// Logisim project main.circ as structural Verilog
module Frontend (
);

  wire topmodule_1_hled_game_1, topmodule_1_hled_game_2, topmodule_1_hled_game_3,
       topmodule_1_hled_keyboard_1, topmodule_1_hled_keyboard_2, topmodule_1_hled_keyboard_3,
       topmodule_1_hstatus_1, topmodule_1_hstatus_2, topmodule_1_hstatus_3, \А_out , \Б_out , \В_out ,
       \Г_out , \Д_out , \Е_out , \Ж_out , \З_out , \И_out , \Й_out , \К_out , \Л_out , \М_out , \Н_out ,
       \О_out , \П_out , \Р_out , \С_out , \Т_out , \У_out , \Ф_out , \Х_out , \Ц_out , \Ч_out , \Ш_out ,
       \Щ_out , \Ъ_out , \Ы_out , \Ь_out , \Э_out , \Ю_out , \Я_out ;
  wire [3:0] topmodule_1_hindicator;
  wire [7:0] topmodule_1_ld_1, topmodule_1_ld_2, topmodule_1_ld_3, topmodule_1_ld_4, topmodule_1_ld_5,
       topmodule_1_ld_6, topmodule_1_ld_7, topmodule_1_ld_8, topmodule_1_ld_9, topmodule_1_ld_10,
       topmodule_1_ld_11, topmodule_1_ld_12, topmodule_1_ld_13, topmodule_1_ld_14, topmodule_1_ld_15,
       topmodule_1_ld_16, topmodule_1_ld_17, topmodule_1_ld_18, topmodule_1_ld_19, topmodule_1_ld_20,
       topmodule_1_ld_21, topmodule_1_ld_22, topmodule_1_ld_23, topmodule_1_ld_24, topmodule_1_ld_25,
       topmodule_1_ld_26, topmodule_1_ld_27, topmodule_1_ld_28, topmodule_1_ld_29, topmodule_1_ld_30,
       topmodule_1_ld_31, topmodule_1_ld_32, topmodule_1_ld_33, topmodule_1_ld_34, topmodule_1_ld_35,
       topmodule_1_ld_36, topmodule_1_ld_37, topmodule_1_ld_38, topmodule_1_ld_39, topmodule_1_ld_40,
       topmodule_1_ld_41, topmodule_1_ld_42, topmodule_1_ld_43, topmodule_1_ld_44, topmodule_1_ld_45,
       topmodule_1_ld_46, topmodule_1_ld_47, topmodule_1_ld_48;
  wire [31:0] topmodule_1_md_1, topmodule_1_md_2, topmodule_1_md_3, topmodule_1_md_4, topmodule_1_md_5,
       topmodule_1_md_6, topmodule_1_md_7, topmodule_1_md_8, topmodule_1_md_9, topmodule_1_md_10,
       topmodule_1_md_11, topmodule_1_md_12, topmodule_1_md_13, topmodule_1_md_14, topmodule_1_md_15,
       topmodule_1_md_16, topmodule_1_md_17, topmodule_1_md_18, topmodule_1_md_19, topmodule_1_md_20,
       topmodule_1_md_21, topmodule_1_md_22, topmodule_1_md_23, topmodule_1_md_24, topmodule_1_md_25,
       topmodule_1_md_26, topmodule_1_md_27, topmodule_1_md_28, topmodule_1_md_29, topmodule_1_md_30,
       topmodule_1_md_31, topmodule_1_md_32;

  TopModule topmodule_1 (
    .k_0(\А_out ), .ld_1(topmodule_1_ld_1), .md_1(topmodule_1_md_1), .md_3(topmodule_1_md_3),
    .md_2(topmodule_1_md_2), .md_4(topmodule_1_md_4), .md_5(topmodule_1_md_5), .md_7(topmodule_1_md_7),
    .md_6(topmodule_1_md_6), .md_8(topmodule_1_md_8), .md_9(topmodule_1_md_9), .md_11(topmodule_1_md_11),
    .md_10(topmodule_1_md_10), .md_12(topmodule_1_md_12), .md_13(topmodule_1_md_13),
    .md_15(topmodule_1_md_15), .md_14(topmodule_1_md_14), .md_16(topmodule_1_md_16),
    .md_17(topmodule_1_md_17), .md_19(topmodule_1_md_19), .md_18(topmodule_1_md_18),
    .md_20(topmodule_1_md_20), .md_21(topmodule_1_md_21), .md_23(topmodule_1_md_23),
    .md_22(topmodule_1_md_22), .md_24(topmodule_1_md_24), .md_25(topmodule_1_md_25),
    .md_27(topmodule_1_md_27), .md_26(topmodule_1_md_26), .md_28(topmodule_1_md_28),
    .md_29(topmodule_1_md_29), .md_31(topmodule_1_md_31), .md_30(topmodule_1_md_30),
    .md_32(topmodule_1_md_32), .k_1(\Б_out ), .k_2(\В_out ), .k_3(\Г_out ), .k_4(\Д_out ), .k_5(\Е_out ),
    .k_6(\Ж_out ), .k_7(\З_out ), .k_8(\И_out ), .k_9(\Й_out ), .k_10(\К_out ), .k_11(\Л_out ),
    .k_12(\М_out ), .k_13(\Н_out ), .k_31(\Я_out ), .k_14(\О_out ), .k_15(\П_out ), .k_16(\Р_out ),
    .k_17(\С_out ), .k_18(\Т_out ), .k_19(\У_out ), .k_20(\Ф_out ), .k_21(\Х_out ), .k_22(\Ц_out ),
    .k_23(\Ч_out ), .k_24(\Ш_out ), .k_25(\Щ_out ), .k_26(\Ъ_out ), .k_27(\Ы_out ), .k_28(\Ь_out ),
    .k_29(\Э_out ), .k_30(\Ю_out ), .ld_2(topmodule_1_ld_2), .ld_3(topmodule_1_ld_3),
    .ld_4(topmodule_1_ld_4), .ld_5(topmodule_1_ld_5), .ld_6(topmodule_1_ld_6), .ld_7(topmodule_1_ld_7),
    .ld_8(topmodule_1_ld_8), .ld_9(topmodule_1_ld_9), .ld_10(topmodule_1_ld_10), .ld_11(topmodule_1_ld_11),
    .ld_12(topmodule_1_ld_12), .ld_13(topmodule_1_ld_13), .ld_14(topmodule_1_ld_14),
    .ld_15(topmodule_1_ld_15), .ld_16(topmodule_1_ld_16), .ld_17(topmodule_1_ld_17),
    .ld_18(topmodule_1_ld_18), .ld_19(topmodule_1_ld_19), .ld_20(topmodule_1_ld_20),
    .ld_21(topmodule_1_ld_21), .ld_22(topmodule_1_ld_22), .ld_23(topmodule_1_ld_23),
    .ld_24(topmodule_1_ld_24), .ld_25(topmodule_1_ld_25), .ld_26(topmodule_1_ld_26),
    .ld_27(topmodule_1_ld_27), .ld_28(topmodule_1_ld_28), .ld_29(topmodule_1_ld_29),
    .ld_30(topmodule_1_ld_30), .ld_31(topmodule_1_ld_31), .ld_32(topmodule_1_ld_32),
    .ld_33(topmodule_1_ld_33), .ld_34(topmodule_1_ld_34), .ld_35(topmodule_1_ld_35),
    .ld_36(topmodule_1_ld_36), .ld_37(topmodule_1_ld_37), .ld_38(topmodule_1_ld_38),
    .ld_39(topmodule_1_ld_39), .ld_40(topmodule_1_ld_40), .ld_41(topmodule_1_ld_41),
    .ld_42(topmodule_1_ld_42), .ld_43(topmodule_1_ld_43), .ld_44(topmodule_1_ld_44),
    .ld_45(topmodule_1_ld_45), .ld_46(topmodule_1_ld_46), .ld_47(topmodule_1_ld_47),
    .ld_48(topmodule_1_ld_48), .HINDICATOR(topmodule_1_hindicator), .HLED_GAME_2(topmodule_1_hled_game_2),
    .HLED_KEYBOARD_1(topmodule_1_hled_keyboard_1), .HLED_GAME_3(topmodule_1_hled_game_3),
    .HLED_GAME_1(topmodule_1_hled_game_1), .HLED_KEYBOARD_2(topmodule_1_hled_keyboard_2),
    .HLED_KEYBOARD_3(topmodule_1_hled_keyboard_3), .HSTATUS_1(topmodule_1_hstatus_1),
    .HSTATUS_2(topmodule_1_hstatus_2), .HSTATUS_3(topmodule_1_hstatus_3));
  DotMatrix #(.matrixcols(24), .matrixrows(8)) dotmatrix_1 (
    .col0(topmodule_1_ld_1), .col1(topmodule_1_ld_2), .col2(topmodule_1_ld_3), .col3(topmodule_1_ld_4),
    .col4(topmodule_1_ld_5), .col5(topmodule_1_ld_6), .col6(topmodule_1_ld_7), .col7(topmodule_1_ld_8),
    .col8(topmodule_1_ld_9), .col9(topmodule_1_ld_10), .col10(topmodule_1_ld_11), .col11(topmodule_1_ld_12),
    .col12(topmodule_1_ld_13), .col13(topmodule_1_ld_14), .col14(topmodule_1_ld_15),
    .col15(topmodule_1_ld_16), .col16(topmodule_1_ld_17), .col17(topmodule_1_ld_18),
    .col18(topmodule_1_ld_19), .col19(topmodule_1_ld_20), .col20(topmodule_1_ld_21),
    .col21(topmodule_1_ld_22), .col22(topmodule_1_ld_23), .col23(topmodule_1_ld_24));
  DotMatrix #(.inputtype("row"), .matrixcols(32), .matrixrows(32)) dotmatrix_2 (
    .row0(topmodule_1_md_1), .row1(topmodule_1_md_2), .row2(topmodule_1_md_3), .row3(topmodule_1_md_4),
    .row4(topmodule_1_md_5), .row5(topmodule_1_md_6), .row6(topmodule_1_md_7), .row7(topmodule_1_md_8),
    .row8(topmodule_1_md_9), .row9(topmodule_1_md_10), .row10(topmodule_1_md_11), .row11(topmodule_1_md_12),
    .row12(topmodule_1_md_13), .row13(topmodule_1_md_14), .row14(topmodule_1_md_15),
    .row15(topmodule_1_md_16), .row16(topmodule_1_md_17), .row17(topmodule_1_md_18),
    .row18(topmodule_1_md_19), .row19(topmodule_1_md_20), .row20(topmodule_1_md_21),
    .row21(topmodule_1_md_22), .row22(topmodule_1_md_23), .row23(topmodule_1_md_24),
    .row24(topmodule_1_md_25), .row25(topmodule_1_md_26), .row26(topmodule_1_md_27),
    .row27(topmodule_1_md_28), .row28(topmodule_1_md_29), .row29(topmodule_1_md_30),
    .row30(topmodule_1_md_31), .row31(topmodule_1_md_32));
  Button \u_Й  (.out(\Й_out ));
  Button \u_Ц  (.out(\Ц_out ));
  Button \u_Ф  (.out(\Ф_out ));
  Button \u_Ы  (.out(\Ы_out ));
  Button \u_Я  (.out(\Я_out ));
  Button \u_Ч  (.out(\Ч_out ));
  Button \u_К  (.out(\К_out ));
  Button \u_У  (.out(\У_out ));
  Button \u_Е  (.out(\Е_out ));
  Button \u_П  (.out(\П_out ));
  Button \u_В  (.out(\В_out ));
  Button \u_А  (.out(\А_out ));
  Button \u_М  (.out(\М_out ));
  Button \u_С  (.out(\С_out ));
  DotMatrix #(.matrixcols(24), .matrixrows(8)) dotmatrix_3 (
    .col0(topmodule_1_ld_25), .col1(topmodule_1_ld_26), .col2(topmodule_1_ld_27), .col3(topmodule_1_ld_28),
    .col4(topmodule_1_ld_29), .col5(topmodule_1_ld_30), .col6(topmodule_1_ld_31), .col7(topmodule_1_ld_32),
    .col8(topmodule_1_ld_33), .col9(topmodule_1_ld_34), .col10(topmodule_1_ld_35), .col11(topmodule_1_ld_36),
    .col12(topmodule_1_ld_37), .col13(topmodule_1_ld_38), .col14(topmodule_1_ld_39),
    .col15(topmodule_1_ld_40), .col16(topmodule_1_ld_41), .col17(topmodule_1_ld_42),
    .col18(topmodule_1_ld_43), .col19(topmodule_1_ld_44), .col20(topmodule_1_ld_45),
    .col21(topmodule_1_ld_46), .col22(topmodule_1_ld_47), .col23(topmodule_1_ld_48));
  Button \u_Н  (.out(\Н_out ));
  Button \u_Ш  (.out(\Ш_out ));
  Button \u_Г  (.out(\Г_out ));
  Button \u_О  (.out(\О_out ));
  Button \u_Р  (.out(\Р_out ));
  Button \u_Т  (.out(\Т_out ));
  Button \u_И  (.out(\И_out ));
  Button \u_Ь  (.out(\Ь_out ));
  Button \u_З  (.out(\З_out ));
  Button \u_Щ  (.out(\Щ_out ));
  Button \u_Л  (.out(\Л_out ));
  Button \u_Ж  (.out(\Ж_out ));
  Button \u_Д  (.out(\Д_out ));
  Button \u_Ю  (.out(\Ю_out ));
  Button \u_Б  (.out(\Б_out ));
  Hex_Digit_Display hex_digit_display_1 (.value(topmodule_1_hindicator));  // open: dp
  LED led_1 (.in(topmodule_1_hstatus_1));
  LED led_2 (.in(topmodule_1_hstatus_2));
  LED led_3 (.in(topmodule_1_hstatus_3));
  LED led_4 (.in(topmodule_1_hled_keyboard_1));
  LED led_5 (.in(topmodule_1_hled_keyboard_2));
  LED led_6 (.in(topmodule_1_hled_keyboard_3));
  LED led_7 (.in(topmodule_1_hled_game_1));
  LED led_8 (.in(topmodule_1_hled_game_2));
  LED led_9 (.in(topmodule_1_hled_game_3));
  Button \u_Х  (.out(\Х_out ));
  Button \u_Ъ  (.out(\Ъ_out ));
  Button \u_Э  (.out(\Э_out ));

  // Notes on the sheet:
  //   G - waiting
  //   Y - halted
  //   CdM
  //   R - fault
endmodule

module TopModule (
  input  k_15,
  input  k_16,
  input  k_14,
  input  k_17,
  input  k_13,
  input  k_18,
  input  k_12,
  input  k_19,
  input  k_11,
  input  k_20,
  input  k_10,
  input  k_21,
  input  k_9,
  input  k_22,
  input  k_8,
  input  k_23,
  input  k_7,
  input  k_24,
  input  k_6,
  input  k_25,
  input  k_5,
  input  k_26,
  input  k_4,
  input  k_27,
  input  k_3,
  input  k_28,
  input  k_2,
  input  k_29,
  input  k_1,
  input  k_30,
  input  k_0,
  input  k_31,
  output HLED_GAME_1,
  output HSTATUS_1,
  output HLED_GAME_2,
  output HSTATUS_2,
  output HLED_GAME_3,
  output HSTATUS_3,
  output [3:0] HINDICATOR,
  output HLED_KEYBOARD_1,
  output HLED_KEYBOARD_2,
  output HLED_KEYBOARD_3,
  output [31:0] md_1,
  output [31:0] md_32,
  output [7:0] ld_1,
  output [7:0] ld_48,
  output [7:0] ld_2,
  output [7:0] ld_47,
  output [7:0] ld_3,
  output [7:0] ld_46,
  output [31:0] md_2,
  output [31:0] md_31,
  output [7:0] ld_4,
  output [7:0] ld_45,
  output [7:0] ld_5,
  output [7:0] ld_44,
  output [7:0] ld_6,
  output [7:0] ld_43,
  output [31:0] md_3,
  output [31:0] md_30,
  output [7:0] ld_7,
  output [7:0] ld_42,
  output [7:0] ld_8,
  output [7:0] ld_41,
  output [7:0] ld_9,
  output [7:0] ld_40,
  output [7:0] ld_10,
  output [7:0] ld_39,
  output [31:0] md_4,
  output [31:0] md_29,
  output [7:0] ld_11,
  output [7:0] ld_38,
  output [7:0] ld_12,
  output [7:0] ld_37,
  output [7:0] ld_13,
  output [7:0] ld_36,
  output [31:0] md_5,
  output [31:0] md_28,
  output [7:0] ld_14,
  output [7:0] ld_35,
  output [7:0] ld_15,
  output [7:0] ld_34,
  output [7:0] ld_16,
  output [7:0] ld_33,
  output [7:0] ld_17,
  output [7:0] ld_32,
  output [31:0] md_6,
  output [31:0] md_27,
  output [7:0] ld_18,
  output [7:0] ld_31,
  output [7:0] ld_19,
  output [7:0] ld_30,
  output [7:0] ld_20,
  output [7:0] ld_29,
  output [31:0] md_7,
  output [31:0] md_26,
  output [7:0] ld_21,
  output [7:0] ld_28,
  output [7:0] ld_22,
  output [7:0] ld_27,
  output [7:0] ld_23,
  output [7:0] ld_26,
  output [7:0] ld_24,
  output [7:0] ld_25,
  output [31:0] md_8,
  output [31:0] md_25,
  output [31:0] md_9,
  output [31:0] md_24,
  output [31:0] md_10,
  output [31:0] md_23,
  output [31:0] md_11,
  output [31:0] md_22,
  output [31:0] md_12,
  output [31:0] md_21,
  output [31:0] md_13,
  output [31:0] md_20,
  output [31:0] md_14,
  output [31:0] md_19,
  output [31:0] md_15,
  output [31:0] md_18,
  output [31:0] md_16,
  output [31:0] md_17
);

  wire demultiplexer_1_out0, demultiplexer_1_out1, demultiplexer_1_out2, demultiplexer_1_out3,
       demultiplexer_1_out4, demultiplexer_1_out5, demultiplexer_1_out6, demultiplexer_1_out7, HCLK,
       HUPT_MAINDISPLAY, HUPT_SUBDISPLAY_1, HUPT_SUBDISPLAY_2, HUPT_SUBDISPLAY_3, HUPT_SUBDISPLAY_4,
       HUPT_SUBDISPLAY_5, HUPT_SUBDISPLAY_6, master_cdm_1_hiack, master_cdm_1_hmemory, master_cdm_1_hsize,
       master_cdm_1_hwrite, slave_keyboard_1_hirq;
  wire [2:0] interconnect_bitselector_1_hbits_2_0;
  wire [7:0] interconnect_bitselector_1_haddr_7_0;
  wire [15:0] HWDATA_15_0, master_cdm_1_haddr_15_0, multiplexer_1_out,
       slave_indicatorcontroller_1_hrdata_15_0, slave_keyboard_1_hrdata_15_0,
       slave_maindisplay_1_hrdata_15_0, slave_ram_1_hrdata_15_0, slave_random_1_hrdata_15_0,
       slave_rulescontroller_1_hrdata_15_0, slave_subdisplay_1_hrdata_15_0, slave_terminal_1_hrdata_15_0;

  Master_CdM master_cdm_1 (
    .HCLK(HCLK), .HIRQ(slave_keyboard_1_hirq), .HIRQ_VECTOR(6'b000101), .HRDATA_15_0(multiplexer_1_out),
    .HMEMORY(master_cdm_1_hmemory), .HWRITE(master_cdm_1_hwrite), .HSIZE(master_cdm_1_hsize),
    .HADDR_15_0(master_cdm_1_haddr_15_0), .HWDATA_15_0(HWDATA_15_0), .HIAck(master_cdm_1_hiack),
    .HSTATUS_1(HSTATUS_1), .HSTATUS_2(HSTATUS_2), .HSTATUS_3(HSTATUS_3));  // open: HEXC, HEXC_VECTOR
  Clock clock_1 (.out(HCLK));
  Slave_SubDisplay slave_subdisplay_1 (
    .HUPT_1(HUPT_SUBDISPLAY_1), .HUPT_2(HUPT_SUBDISPLAY_2), .HUPT_3(HUPT_SUBDISPLAY_3),
    .HUPT_4(HUPT_SUBDISPLAY_4), .HUPT_5(HUPT_SUBDISPLAY_5), .HUPT_6(HUPT_SUBDISPLAY_6),
    .HWDATA_15_0(HWDATA_15_0), .HRDATA_15_0(slave_subdisplay_1_hrdata_15_0), .HWRITE(master_cdm_1_hwrite),
    .HCLK(HCLK), .HSEL(demultiplexer_1_out6), .HADDR_7_0(interconnect_bitselector_1_haddr_7_0),
    .HSIZE(master_cdm_1_hsize), .HLINE_1(ld_1), .HLINE_13(ld_13), .HLINE_25(ld_25), .HLINE_37(ld_37),
    .HLINE_2(ld_2), .HLINE_14(ld_14), .HLINEne_26(ld_26), .HLINE_38(ld_38), .HLINE_3(ld_3), .HLINE_15(ld_15),
    .HLINE_27(ld_27), .HLINE_39(ld_39), .HLINE_4(ld_4), .HLINE_16(ld_16), .HLINE_28(ld_28), .HLINE_40(ld_40),
    .HLINE_5(ld_5), .HLINE_17(ld_17), .HLINE_29(ld_29), .HLINE_41(ld_41), .HLINE_6(ld_6), .HLINE_18(ld_18),
    .HLINE_30(ld_30), .HLINE_42(ld_42), .HLINE_7(ld_7), .HLINE_19(ld_19), .HLINE_31(ld_31), .HLINE_43(ld_43),
    .HLINE_8(ld_8), .HLINE_20(ld_20), .HLINE_32(ld_32), .HLINE_44(ld_44), .HLINE_9(ld_9), .HLINE_21(ld_21),
    .HLINE_33(ld_33), .HLINE_45(ld_45), .HLINE_10(ld_10), .HLINE_22(ld_22), .HLINE_34(ld_34),
    .HLINE_46(ld_46), .HLINE_11(ld_11), .HLINE_23(ld_23), .HLINE_35(ld_35), .HLINE_47(ld_47),
    .HLINE_12(ld_12), .HLINE_24(ld_24), .HLINE_36(ld_36), .HLINE_48(ld_48));  // open: HRESP, HRESET
  Interconnect_BitSelector interconnect_bitselector_1 (
    .HBITS_2_0(interconnect_bitselector_1_hbits_2_0), .HADDR_15_0(master_cdm_1_haddr_15_0),
    .HADDR_7_0(interconnect_bitselector_1_haddr_7_0));
  Demultiplexer #(.select(3)) demultiplexer_1 (
    .out0(demultiplexer_1_out0), .out1(demultiplexer_1_out1), .out2(demultiplexer_1_out2),
    .out3(demultiplexer_1_out3), .out4(demultiplexer_1_out4), .out5(demultiplexer_1_out5),
    .out6(demultiplexer_1_out6), .out7(demultiplexer_1_out7), .in(master_cdm_1_hmemory),
    .sel(interconnect_bitselector_1_hbits_2_0));  // open: en
  Multiplexer #(.select(3), .width(16), .enable("false")) multiplexer_1 (
    .in0(slave_ram_1_hrdata_15_0), .in1(slave_terminal_1_hrdata_15_0),
    .in2(slave_indicatorcontroller_1_hrdata_15_0), .in3(slave_random_1_hrdata_15_0),
    .in4(slave_keyboard_1_hrdata_15_0), .in5(slave_rulescontroller_1_hrdata_15_0),
    .in6(slave_subdisplay_1_hrdata_15_0), .in7(slave_maindisplay_1_hrdata_15_0), .out(multiplexer_1_out),
    .sel(interconnect_bitselector_1_hbits_2_0));
  Slave_Keyboard slave_keyboard_1 (
    .HKEY_0(k_0), .HKEY_1(k_1), .HKEY_2(k_2), .HKEY_3(k_3), .HKEY_4(k_4), .HKEY_5(k_5), .HKEY_6(k_6),
    .HKEY_7(k_7), .HKEY_8(k_8), .HKEY_9(k_9), .HKEY_10(k_10), .HKEY_11(k_11), .HKEY_12(k_12), .HKEY_13(k_13),
    .HKEY_14(k_14), .HKEY_15(k_15), .HKEY_16(k_16), .HKEY_17(k_17), .HKEY_18(k_18), .HKEY_19(k_19),
    .HKEY_20(k_20), .HKEY_21(k_21), .HKEY_22(k_22), .HKEY_23(k_23), .HKEY_24(k_24), .HKEY_25(k_25),
    .HKEY_26(k_26), .HKEY_27(k_27), .HKEY_28(k_28), .HKEY_29(k_29), .HKEY_30(k_30), .HKEY_31(k_31),
    .HWDATA_15_0(HWDATA_15_0), .HWRITE(master_cdm_1_hwrite), .HSEL(demultiplexer_1_out4),
    .HADDR_7_0(interconnect_bitselector_1_haddr_7_0), .HSIZE(master_cdm_1_hsize), .HCLK(HCLK),
    .HIAck(master_cdm_1_hiack), .HRDATA_15_0(slave_keyboard_1_hrdata_15_0), .HIRQ(slave_keyboard_1_hirq));  // open: HRESP, HRESET
  Slave_Random slave_random_1 (
    .HWDATA_15_0(HWDATA_15_0), .HWRITE(master_cdm_1_hwrite), .HCLK(HCLK), .HSEL(demultiplexer_1_out3),
    .HADDR_7_0(interconnect_bitselector_1_haddr_7_0), .HSIZE(master_cdm_1_hsize),
    .HRDATA_15_0(slave_random_1_hrdata_15_0));  // open: HRESET, HRESP
  Slave_RulesController slave_rulescontroller_1 (
    .HWDATA_15_0(HWDATA_15_0), .HWRITE(master_cdm_1_hwrite), .HCLK(HCLK), .HSEL(demultiplexer_1_out5),
    .HADDR_7_0(interconnect_bitselector_1_haddr_7_0), .HSIZE(master_cdm_1_hsize),
    .HRDATA_15_0(slave_rulescontroller_1_hrdata_15_0), .HUPT_MAINDISPLAY(HUPT_MAINDISPLAY),
    .HUPT_SUBDISPLAY_1(HUPT_SUBDISPLAY_1), .HUPT_SUBDISPLAY_2(HUPT_SUBDISPLAY_2),
    .HUPT_SUBDISPLAY_3(HUPT_SUBDISPLAY_3), .HUPT_SUBDISPLAY_4(HUPT_SUBDISPLAY_4),
    .HUPT_SUBDISPLAY_5(HUPT_SUBDISPLAY_5), .HUPT_SUBDISPLAY_6(HUPT_SUBDISPLAY_6));  // open: HRESET, HRESP
  Slave_RAM slave_ram_1 (
    .HADDR_15_0(master_cdm_1_haddr_15_0), .HSIZE(master_cdm_1_hsize), .HSEL(demultiplexer_1_out0),
    .HCLK(HCLK), .HWDATA_15_0(HWDATA_15_0), .HWRITE(master_cdm_1_hwrite),
    .HRDATA_15_0(slave_ram_1_hrdata_15_0));  // open: HRESET, HRESP
  Slave_MainDisplay slave_maindisplay_1 (
    .line_1(md_1), .line_2(md_2), .line_3(md_3), .line_4(md_4), .line_5(md_5), .line_6(md_6), .line_7(md_7),
    .line_8(md_8), .line_9(md_9), .line_10(md_10), .line_11(md_11), .line_12(md_12), .line_13(md_13),
    .line_14(md_14), .line_15(md_15), .line_16(md_16), .line_17(md_17), .line_18(md_18), .line_19(md_19),
    .line_20(md_20), .line_21(md_21), .line_22(md_22), .line_23(md_23), .line_24(md_24), .line_25(md_25),
    .line_26(md_26), .line_27(md_27), .line_28(md_28), .line_29(md_29), .line_30(md_30), .line_31(md_31),
    .line_32(md_32), .HWDATA_15_0(HWDATA_15_0), .HRDATA_15_0(slave_maindisplay_1_hrdata_15_0),
    .HWRITE(master_cdm_1_hwrite), .HCLK(HCLK), .HSEL(demultiplexer_1_out7),
    .HADDR_7_0(interconnect_bitselector_1_haddr_7_0), .HSIZE(master_cdm_1_hsize), .HUPT(HUPT_MAINDISPLAY));  // open: HRESP, HRESET
  Slave_Terminal slave_terminal_1 (
    .HWDATA_15_0(HWDATA_15_0), .HWRITE(master_cdm_1_hwrite), .HCLK(HCLK), .HSEL(demultiplexer_1_out1),
    .HADDR_7_0(interconnect_bitselector_1_haddr_7_0), .HSIZE(master_cdm_1_hsize),
    .HRDATA_15_0(slave_terminal_1_hrdata_15_0));  // open: HRESET, HRESP
  Slave_IndicatorController slave_indicatorcontroller_1 (
    .HWDATA_15_0(HWDATA_15_0), .HWRITE(master_cdm_1_hwrite), .HCLK(HCLK), .HSEL(demultiplexer_1_out2),
    .HADDR_7_0(interconnect_bitselector_1_haddr_7_0), .HSIZE(master_cdm_1_hsize),
    .HRDATA_15_0(slave_indicatorcontroller_1_hrdata_15_0), .HINDICATOR(HINDICATOR),
    .HLED_GAME_1(HLED_GAME_1), .HLED_KEYBOARD_3(HLED_KEYBOARD_3), .HLED_GAME_2(HLED_GAME_2),
    .HLED_GAME_3(HLED_GAME_3), .HLED_KEYBOARD_2(HLED_KEYBOARD_2), .HLED_KEYBOARD_1(HLED_KEYBOARD_1));  // open: HRESET, HRESP
  // also tied to GND on the sheet: {slave_terminal_1_hrdata_15_0[0], slave_terminal_1_hrdata_15_0[1], slave_terminal_1_hrdata_15_0[2], slave_terminal_1_hrdata_15_0[3], slave_terminal_1_hrdata_15_0[4], slave_terminal_1_hrdata_15_0[5], slave_terminal_1_hrdata_15_0[6], slave_terminal_1_hrdata_15_0[7], slave_terminal_1_hrdata_15_0[8], slave_terminal_1_hrdata_15_0[9], slave_terminal_1_hrdata_15_0[10], slave_terminal_1_hrdata_15_0[11], slave_terminal_1_hrdata_15_0[12], slave_terminal_1_hrdata_15_0[13], slave_terminal_1_hrdata_15_0[14], slave_terminal_1_hrdata_15_0[15]}

  // Notes on the sheet:
  //   HWRITE
  //   HIRQ
  //   HRDATA[15:0]
  //   HSEL_SUBDISPLAY
  //   HSEL_SUBDISPLAY
  //   HADDR[7:0]
  //   HSIZE
  //   HWDATA[15:0]
  //   MASTER
  //   HADDR[15:0]
  //   HWRITE
  //   HSIZE
  //   HMEMORY
  //   HIAck
  //   HWDATA[15:0]
  //   HWDATA[15:0]
  //   HWRITE
  //   HSIZE
  //   HADDR[7:0]
  //   HADDR[15:0]
  //   HADDR[7:0]
  //   HADDR[15:0]
  //   INTERCONNECT
  //   HMEMORY
  //   HRDATA[15:0]
  //   HRDATA_SUBDISPLAY[15:0]
  //   SLAVE_7
  //   HRDATA_RAM[15:0]
  //   HSEL_SUBDISPLAY
  //   HADDR[7:0]
  //   HSEL_HEYBOARD
  //   HSIZE
  //   HADDR[7:0]
  //   HWRITE
  //   HSIZE
  //   HSEL_RAM
  //   HSEL_MAINDISPLAY
  //   HADDR[7:0]
  //   HWRITE
  //   HWDATA[15:0]
  //   HRDATA_KEYBOARD[15:0]
  //   HRDATA_RANDOM[15:0]
  //   SLAVE_6
  //   HRDATA_RAM[15:0]
  //   HRDATA_MAINDISPLAY[15:0]
  //   HSEL_RANDOM
  //   HADDR[7:0]
  //   HWRITE
  //   HSIZE
  //   HWDATA[15:0]
  //   HSEL_RULES
  //   HADDR[7:0]
  //   HSIZE
  //   HWDATA[15:0]
  //   HSEL_RAM
  //   HADDR[15:0]
  //   HWRITE
  //   HSIZE
  //   HWDATA[15:0]
  //   HIRQ
  //   HWRITE
  //   SLAVE_5
  //   SLAVE_4
  //   HRDATA_RANDOM[15:0]
  //   HRDATA_RULES[15:0]
  //   SLAVE_1
  //   HRDATA_RAM[15:0]
  //   HIAck
  //   HSEL_TERMINAL
  //   HADDR[7:0]
  //   HWRITE
  //   HSIZE
  //   HWDATA[15:0]
  //   HWDATA[15:0]
  //   SLAVE_8
  //   HWDATA[15:0]
  //   HSEL_INDICATORS
  //   HADDR[7:0]
  //   HWRITE
  //   HSIZE
  //   SLAVE_3
  //   HRDATA_MAINDISPLAY[15:0]
  //   SLAVE_2
endmodule

module Master_CdM (
  input  HCLK,
  input  HIRQ,
  input  [5:0] HIRQ_VECTOR,
  input  HEXC,
  input  [5:0] HEXC_VECTOR,
  input  [15:0] HRDATA_15_0,
  output HMEMORY,
  output HWRITE,
  output HSIZE,
  output [15:0] HADDR_15_0,
  output [15:0] HWDATA_15_0,
  output HIAck,
  output HSTATUS_1,
  output HSTATUS_2,
  output HSTATUS_3
);

  wire cdm_16_1_p6, cdm_16_1_p7, cdm_16_1_p9, cdm_16_1_p10, cdm_16_1_p11, cdm_16_1_p13, cdm_16_1_p14,
       cdm_16_1_p15, cdm_16_1_p16, cdm_16_1_p17, cdm_16_1_p18, cdm_16_1_p20;
  wire [1:0] cdm_16_1_p12;
  wire [5:0] cdm_16_1_p2;

  // Debugger debugger_1: pin names not known
  Pull_Resistor pull_resistor_1 (.node(HRDATA_15_0));
  // Probe on cdm_16_1_p14
  // Probe on cdm_16_1_p11
  // Probe on cdm_16_1_p9
  // Probe on cdm_16_1_p6
  // Probe on cdm_16_1_p15
  // Probe on cdm_16_1_p13
  // Probe on cdm_16_1_p10
  // Probe on cdm_16_1_p7
  // CdM_16 cdm_16_1: pin names not known; wires that end beside it: HIRQ, cdm_16_1_p2, HIAck, HEXC, HEXC_VECTOR, cdm_16_1_p6, cdm_16_1_p7, HCLK, cdm_16_1_p9, cdm_16_1_p10, cdm_16_1_p11, cdm_16_1_p12, cdm_16_1_p13, cdm_16_1_p14, cdm_16_1_p15, cdm_16_1_p16, cdm_16_1_p17, cdm_16_1_p18, HMEMORY, cdm_16_1_p20, HSIZE, HADDR_15_0, HWDATA_15_0, HRDATA_15_0
  assign cdm_16_1_p2 = HIAck ? HIRQ_VECTOR : 6'bz;  // Controlled_Buffer controlled_buffer_1
  // Probe on cdm_16_1_p15
  // Probe on cdm_16_1_p17
  // Probe on cdm_16_1_p16
  // Probe on cdm_16_1_p18
  Pull_Resistor pull_resistor_2 (.node(HMEMORY));
  Pull_Resistor pull_resistor_3 (.node(cdm_16_1_p20));
  not not_1 (HWRITE, cdm_16_1_p20);
  Pull_Resistor pull_resistor_4 (.node(HADDR_15_0));
  Pull_Resistor pull_resistor_5 (.node(HWDATA_15_0));
  Decoder #(.select(2), .enable("false")) decoder_1 (
    .out1(HSTATUS_1), .out2(HSTATUS_2), .out3(HSTATUS_3), .sel(cdm_16_1_p12));  // open: out0

  // Notes on the sheet:
  //   Master CdM is the central processor of the platform
endmodule

module Interconnect_BitSelector (
  input  [15:0] HADDR_15_0,
  output [7:0] HADDR_7_0,
  output [2:0] HBITS_2_0
);

  wire and_1_out, and_2_out, and_3_out, and_4_out, and_5_out, and_6_out, and_7_out, and_8_out, not_5_out,
       or_1_out;
  wire [7:0] not_1_out, not_2_out, not_3_out, not_4_out, not_6_out, not_7_out, not_8_out;

  and and_1 (and_1_out, HADDR_15_0[7], ~HADDR_15_0[0], and_3_out);  // AND_Gate
  or or_1 (or_1_out, HADDR_15_0[5], HADDR_15_0[4]);
  and and_2 (and_2_out, or_1_out, ~HADDR_15_0[7], HADDR_15_0[6], ~HADDR_15_0[0], and_3_out);  // AND_Gate
  and and_3 (and_3_out, HADDR_15_0[8], HADDR_15_0[9], HADDR_15_0[10], HADDR_15_0[11], HADDR_15_0[12], HADDR_15_0[13], HADDR_15_0[14], HADDR_15_0[15]);
  and and_4 (and_4_out, ~HADDR_15_0[7], HADDR_15_0[6], ~HADDR_15_0[5], ~HADDR_15_0[4], HADDR_15_0[3], HADDR_15_0[2], HADDR_15_0[1], ~HADDR_15_0[0], and_3_out);  // AND_Gate
  and and_5 (and_5_out, ~HADDR_15_0[7], HADDR_15_0[6], ~HADDR_15_0[5], ~HADDR_15_0[4], HADDR_15_0[3], HADDR_15_0[2], ~HADDR_15_0[1], ~HADDR_15_0[0], and_3_out);  // AND_Gate
  and and_6 (and_6_out, ~HADDR_15_0[7], HADDR_15_0[6], ~HADDR_15_0[5], ~HADDR_15_0[4], HADDR_15_0[3], ~HADDR_15_0[2], HADDR_15_0[1], ~HADDR_15_0[0], and_3_out);  // AND_Gate
  and and_7 (and_7_out, ~HADDR_15_0[7], HADDR_15_0[6], ~HADDR_15_0[5], ~HADDR_15_0[4], HADDR_15_0[3], ~HADDR_15_0[2], ~HADDR_15_0[1], ~HADDR_15_0[0], and_3_out);  // AND_Gate
  and and_8 (and_8_out, ~HADDR_15_0[7], HADDR_15_0[6], ~HADDR_15_0[5], ~HADDR_15_0[4], HADDR_15_0[3], ~HADDR_15_0[2], ~HADDR_15_0[1], ~HADDR_15_0[0], and_3_out);  // AND_Gate
  assign not_1_out = ~not_2_out;  // NOT_Gate not_1, 8 bits wide
  assign not_2_out = ~HADDR_15_0[7:0];  // NOT_Gate not_2, 8 bits wide
  assign not_3_out = ~not_1_out;  // NOT_Gate not_3, 8 bits wide
  assign not_4_out = ~not_3_out;  // NOT_Gate not_4, 8 bits wide
  not not_5 (not_5_out, and_3_out);
  assign not_6_out = ~not_7_out;  // NOT_Gate not_6, 8 bits wide
  assign not_7_out = ~not_4_out;  // NOT_Gate not_7, 8 bits wide
  assign not_8_out = ~not_6_out;  // NOT_Gate not_8, 8 bits wide
  Priority_Encoder priority_encoder_1 (
    .in0(not_5_out), .in1(and_8_out), .in2(and_7_out), .in3(and_6_out), .in4(and_5_out), .in5(and_4_out),
    .in6(and_2_out), .in7(and_1_out), .out(HBITS_2_0));  // open: en_in, gs, en_out
  assign HADDR_7_0 = ~not_8_out;  // NOT_Gate not_9, 8 bits wide
  Pull_Resistor pull_resistor_1 (.node(HBITS_2_0));

  // Notes on the sheet:
  //   HSEL_IO
  //   HADDR_IO[7:0]
  //   HSEL_MAINDISPLAY
  //   HSEL_SUBDISPLAY
  //   HSEL_RULES
  //   HSEL_KEYBOARD
  //   HSEL_RANDOM
  //   Bit selector to distribute slace inclusion
  //   HSEL_INDICATORS
  //   HSEL_TERMINAL
  //   HSEL_RAM
endmodule

module Slave_RAM (
  input  [15:0] HADDR_15_0,
  input  HSIZE,
  input  HSEL,
  input  HCLK,
  input  HRESET,
  input  [15:0] HWDATA_15_0,
  input  HWRITE,
  output [15:0] HRDATA_15_0,
  output HRESP
);

  wire not_1_out, ram_1_p4;
  wire [15:0] controlled_buffer_2_out;

  // Probe on HADDR_15_0
  // Probe on controlled_buffer_2_out
  assign HRDATA_15_0 = not_1_out ? controlled_buffer_2_out : 16'bz;  // Controlled_Buffer controlled_buffer_1
  not not_1 (not_1_out, HWRITE);
  // RAM ram_1: pin names not known; wires that end beside it: HSIZE, HSEL, HCLK, ram_1_p4, HRESET
  assign controlled_buffer_2_out = HWRITE ? HWDATA_15_0 : 16'bz;  // Controlled_Buffer controlled_buffer_2
  not not_2 (ram_1_p4, HWRITE);
  Pull_Resistor pull_resistor_1 (.node(HRESP));

  // Notes on the sheet:
  //   Slave RAM reading instructions, variables, constants for the master
endmodule

module Slave_Terminal (
  input  [15:0] HWDATA_15_0,
  input  HWRITE,
  input  HCLK,
  input  HSEL,
  input  HRESET,
  input  [7:0] HADDR_7_0,
  input  HSIZE,
  output [15:0] HRDATA_15_0,
  output HRESP
);

  wire and_1_out, comparator_1_eq, comparator_2_eq, demultiplexer_1_out0, demultiplexer_1_out1,
       multiplexer_2_out, not_1_out, not_2_out, not_3_out, not_4_out, not_5_out, not_6_out, or_1_out,
       or_2_out;
  wire [6:0] multiplexer_1_out, register_1_q, register_2_q;

  Pull_Resistor pull_resistor_1 (.node(HRDATA_15_0));
  Pull_Resistor pull_resistor_2 (.node(HRESP));
  Pull_Resistor pull_resistor_3 (.node(HRESET));
  and and_1 (and_1_out, HWRITE, HCLK, HSEL);
  TTY #(.rows(16), .cols(64)) tty_1 (.data(multiplexer_1_out), .clk(multiplexer_2_out), .clr(HRESET));  // open: we
  Register #(.width(7)) register_1 (
    .D(HWDATA_15_0[6:0]), .Q(register_1_q), .clk(and_1_out), .clr(or_1_out));  // open: en
  Register #(.width(7)) register_2 (
    .D(HWDATA_15_0[14:8]), .Q(register_2_q), .clk(and_1_out), .clr(or_2_out));  // open: en
  or or_1 (or_1_out, HRESET, demultiplexer_1_out0);
  or or_2 (or_2_out, demultiplexer_1_out1, HRESET);
  Demultiplexer #(.enable("false")) demultiplexer_1 (
    .out0(demultiplexer_1_out0), .out1(demultiplexer_1_out1), .in(multiplexer_2_out), .sel(comparator_1_eq));
  Multiplexer #(.width(7), .enable("false")) multiplexer_1 (
    .in0(register_1_q), .in1(register_2_q), .out(multiplexer_1_out), .sel(comparator_1_eq));
  Multiplexer #(.enable("false")) multiplexer_2 (
    .in0(not_1_out), .in1(not_2_out), .out(multiplexer_2_out), .sel(not_3_out));
  not not_1 (not_1_out, comparator_1_eq);
  not not_2 (not_2_out, comparator_2_eq);
  Comparator #(.width(7)) comparator_1 (.a(register_1_q), .b({7{1'b0}}), .eq(comparator_1_eq));  // open: gt, lt
  Comparator #(.width(7)) comparator_2 (.a({7{1'b0}}), .b(register_2_q), .eq(comparator_2_eq));  // open: gt, lt
  not not_3 (not_3_out, not_4_out);
  not not_4 (not_4_out, not_5_out);
  not not_5 (not_5_out, not_6_out);
  not not_6 (not_6_out, comparator_1_eq);

  // Notes on the sheet:
  //   Slave terminal receiving logs from master
endmodule

module Slave_IndicatorController (
  input  [15:0] HWDATA_15_0,
  input  HWRITE,
  input  HCLK,
  input  HSEL,
  input  HRESET,
  input  [7:0] HADDR_7_0,
  input  HSIZE,
  output HRESP,
  output [15:0] HRDATA_15_0,
  output [3:0] HINDICATOR,
  output HLED_GAME_1,
  output HLED_GAME_2,
  output HLED_GAME_3,
  output HLED_KEYBOARD_1,
  output HLED_KEYBOARD_2,
  output HLED_KEYBOARD_3
);

  wire and_1_out;

  Register #(.width(16)) register_1 (.D(HWDATA_15_0), .Q(HRDATA_15_0), .clk(and_1_out), .clr(HRESET));  // open: en
  and and_1 (and_1_out, HSEL, HCLK, HWRITE);
  // Probe on 16'h3f
  Comparator #(.width(16), .mode("unsigned")) comparator_1 (.a(16'h3f), .b(HRDATA_15_0), .lt(HRESP));  // open: gt, eq
  assign HINDICATOR = {{1{1'b0}}, HRDATA_15_0[2:0]};  // Bit_Extender bit_extender_1
  Decoder #(.select(2), .enable("false")) decoder_1 (
    .out1(HLED_GAME_1), .out2(HLED_GAME_2), .out3(HLED_GAME_3), .sel(HRDATA_15_0[4:3]));  // open: out0
  Decoder #(.select(2), .enable("false")) decoder_2 (
    .out1(HLED_KEYBOARD_1), .out2(HLED_KEYBOARD_2), .out3(HLED_KEYBOARD_3), .sel(HRDATA_15_0[6:5]));  // open: out0

  // Notes on the sheet:
  //   Slave controller of indicator and two LEDs
endmodule

module Slave_Random (
  input  [15:0] HWDATA_15_0,
  input  HWRITE,
  input  HCLK,
  input  HSEL,
  input  HRESET,
  input  [7:0] HADDR_7_0,
  input  HSIZE,
  output [15:0] HRDATA_15_0,
  output HRESP
);

  wire and_1_out;
  wire [7:0] random_1_out;

  and and_1 (and_1_out, HSEL, HCLK);
  Random random_1 (.clk(and_1_out), .out(random_1_out), .clr(HRESET));  // open: next
  assign HRDATA_15_0 = {{8{1'b0}}, random_1_out};  // Bit_Extender bit_extender_1
  Pull_Resistor pull_resistor_1 (.node(HRESP));

  // Notes on the sheet:
  //   Slave random number generator
endmodule

module Slave_Keyboard (
  input  HKEY_0,
  input  HKEY_1,
  input  HKEY_2,
  input  HKEY_3,
  input  HKEY_4,
  input  HKEY_5,
  input  HKEY_6,
  input  HKEY_7,
  input  HKEY_8,
  input  HKEY_9,
  input  HKEY_10,
  input  HKEY_11,
  input  HSIZE,
  input  HKEY_12,
  input  HKEY_13,
  input  HKEY_14,
  input  HKEY_15,
  input  [7:0] HADDR_7_0,
  input  HSEL,
  input  HKEY_16,
  input  HKEY_17,
  input  HKEY_18,
  input  HKEY_19,
  input  HWRITE,
  input  HKEY_20,
  input  HKEY_21,
  input  HKEY_22,
  input  HKEY_23,
  input  [15:0] HWDATA_15_0,
  input  HCLK,
  input  HKEY_24,
  input  HKEY_25,
  input  HKEY_26,
  input  HKEY_27,
  input  HIAck,
  input  HRESET,
  input  HKEY_28,
  input  HKEY_29,
  input  HKEY_30,
  input  HKEY_31,
  output HIRQ,
  output HRESP,
  output [15:0] HRDATA_15_0
);

  wire and_1_out, k_0, k_1, k_2, k_3, k_4, k_5, k_6, k_7, k_8, k_9, k_10, k_11, k_12, k_13, k_14, k_15, k_16,
       k_17, k_18, k_19, k_20, k_21, k_22, k_23, k_24, k_25, k_26, k_27, k_28, k_29, k_30, k_31,
       priority_encoder_1_p19, RESET_KEYS;
  wire [4:0] priority_encoder_1_p17, register_1_q;

  Pull_Resistor pull_resistor_1 (.node(HRESET));
  Pull_Resistor pull_resistor_2 (.node(HIAck));
  or or_1 (RESET_KEYS, and_1_out, HRESET);
  and and_1 (and_1_out, ~HIAck, ~HCLK, HIRQ);  // AND_Gate
  // Priority_Encoder #(.select(5)) priority_encoder_1: pin names not known; wires that end beside it: k_0, k_1, k_2, k_3, k_4, k_5, k_6, k_7, k_8, k_9, k_10, k_11, k_12, k_13, k_14, k_15, priority_encoder_1_p17, k_16, priority_encoder_1_p19, k_17, k_18, k_19, k_20, k_21, k_22, k_23, k_24, k_25, k_26, k_27, k_28, k_29, k_30, k_31
  Pull_Resistor pull_resistor_3 (.node(priority_encoder_1_p19));
  Register #(.width(5)) register_1 (
    .D(priority_encoder_1_p17), .Q(register_1_q), .clk(priority_encoder_1_p19), .clr(HRESET));  // open: en
  and and_2 (HIRQ, priority_encoder_1_p19, HCLK);
  assign HRDATA_15_0 = {{11{1'b0}}, register_1_q};  // Bit_Extender bit_extender_1
  Pull_Resistor pull_resistor_4 (.node(HRESP));
  D_Flip_Flop d_ff_1 (.clk(HKEY_0), .D(HKEY_0), .Q(k_0), .reset(RESET_KEYS));  // open: Qn, preset, en
  D_Flip_Flop d_ff_2 (.clk(HKEY_4), .D(HKEY_4), .Q(k_4), .reset(RESET_KEYS));  // open: Qn, preset, en
  D_Flip_Flop d_ff_3 (.clk(HKEY_8), .D(HKEY_8), .Q(k_8), .reset(RESET_KEYS));  // open: Qn, preset, en
  D_Flip_Flop d_ff_4 (.clk(HKEY_12), .D(HKEY_12), .Q(k_12), .reset(RESET_KEYS));  // open: Qn, preset, en
  D_Flip_Flop d_ff_5 (.clk(HKEY_16), .D(HKEY_16), .Q(k_16), .reset(RESET_KEYS));  // open: Qn, preset, en
  D_Flip_Flop d_ff_6 (.clk(HKEY_20), .D(HKEY_20), .Q(k_20), .reset(RESET_KEYS));  // open: Qn, preset, en
  D_Flip_Flop d_ff_7 (.clk(HKEY_24), .D(HKEY_24), .Q(k_24), .reset(RESET_KEYS));  // open: Qn, preset, en
  D_Flip_Flop d_ff_8 (.clk(HKEY_28), .D(HKEY_28), .Q(k_28), .reset(RESET_KEYS));  // open: Qn, preset, en
  D_Flip_Flop d_ff_9 (.clk(HKEY_1), .D(HKEY_1), .Q(k_1), .reset(RESET_KEYS));  // open: Qn, preset, en
  D_Flip_Flop d_ff_10 (.clk(HKEY_5), .D(HKEY_5), .Q(k_5), .reset(RESET_KEYS));  // open: Qn, preset, en
  D_Flip_Flop d_ff_11 (.clk(HKEY_9), .D(HKEY_9), .Q(k_9), .reset(RESET_KEYS));  // open: Qn, preset, en
  D_Flip_Flop d_ff_12 (.clk(HKEY_13), .D(HKEY_13), .Q(k_13), .reset(RESET_KEYS));  // open: Qn, preset, en
  D_Flip_Flop d_ff_13 (.clk(HKEY_17), .D(HKEY_17), .Q(k_17), .reset(RESET_KEYS));  // open: Qn, preset, en
  D_Flip_Flop d_ff_14 (.clk(HKEY_21), .D(HKEY_21), .Q(k_21), .reset(RESET_KEYS));  // open: Qn, preset, en
  D_Flip_Flop d_ff_15 (.clk(HKEY_25), .D(HKEY_25), .Q(k_25), .reset(RESET_KEYS));  // open: Qn, preset, en
  D_Flip_Flop d_ff_16 (.clk(HKEY_29), .D(HKEY_29), .Q(k_29), .reset(RESET_KEYS));  // open: Qn, preset, en
  D_Flip_Flop d_ff_17 (.clk(HKEY_2), .D(HKEY_2), .Q(k_2), .reset(RESET_KEYS));  // open: Qn, preset, en
  D_Flip_Flop d_ff_18 (.clk(HKEY_6), .D(HKEY_6), .Q(k_6), .reset(RESET_KEYS));  // open: Qn, preset, en
  D_Flip_Flop d_ff_19 (.clk(HKEY_10), .D(HKEY_10), .Q(k_10), .reset(RESET_KEYS));  // open: Qn, preset, en
  D_Flip_Flop d_ff_20 (.clk(HKEY_14), .D(HKEY_14), .Q(k_14), .reset(RESET_KEYS));  // open: Qn, preset, en
  D_Flip_Flop d_ff_21 (.clk(HKEY_18), .D(HKEY_18), .Q(k_18), .reset(RESET_KEYS));  // open: Qn, preset, en
  D_Flip_Flop d_ff_22 (.clk(HKEY_22), .D(HKEY_22), .Q(k_22), .reset(RESET_KEYS));  // open: Qn, preset, en
  D_Flip_Flop d_ff_23 (.clk(HKEY_26), .D(HKEY_26), .Q(k_26), .reset(RESET_KEYS));  // open: Qn, preset, en
  D_Flip_Flop d_ff_24 (.clk(HKEY_30), .D(HKEY_30), .Q(k_30), .reset(RESET_KEYS));  // open: Qn, preset, en
  D_Flip_Flop d_ff_25 (.clk(HKEY_3), .D(HKEY_3), .Q(k_3), .reset(RESET_KEYS));  // open: Qn, preset, en
  D_Flip_Flop d_ff_26 (.clk(HKEY_7), .D(HKEY_7), .Q(k_7), .reset(RESET_KEYS));  // open: Qn, preset, en
  D_Flip_Flop d_ff_27 (.clk(HKEY_11), .D(HKEY_11), .Q(k_11), .reset(RESET_KEYS));  // open: Qn, preset, en
  D_Flip_Flop d_ff_28 (.clk(HKEY_15), .D(HKEY_15), .Q(k_15), .reset(RESET_KEYS));  // open: Qn, preset, en
  D_Flip_Flop d_ff_29 (.clk(HKEY_19), .D(HKEY_19), .Q(k_19), .reset(RESET_KEYS));  // open: Qn, preset, en
  D_Flip_Flop d_ff_30 (.clk(HKEY_23), .D(HKEY_23), .Q(k_23), .reset(RESET_KEYS));  // open: Qn, preset, en
  D_Flip_Flop d_ff_31 (.clk(HKEY_27), .D(HKEY_27), .Q(k_27), .reset(RESET_KEYS));  // open: Qn, preset, en
  D_Flip_Flop d_ff_32 (.clk(HKEY_31), .D(HKEY_31), .Q(k_31), .reset(RESET_KEYS));  // open: Qn, preset, en

  // Notes on the sheet:
  //   Keyboard slave that tracks the last key pressed
endmodule

module Slave_RulesController (
  input  [15:0] HWDATA_15_0,
  input  HWRITE,
  input  HCLK,
  input  HSEL,
  input  HRESET,
  input  [7:0] HADDR_7_0,
  input  HSIZE,
  output HRESP,
  output [15:0] HRDATA_15_0,
  output HUPT_MAINDISPLAY,
  output HUPT_SUBDISPLAY_6,
  output HUPT_SUBDISPLAY_5,
  output HUPT_SUBDISPLAY_4,
  output HUPT_SUBDISPLAY_3,
  output HUPT_SUBDISPLAY_2,
  output HUPT_SUBDISPLAY_1
);

  wire and_1_out;

  Register #(.width(16)) register_1 (.D(HWDATA_15_0), .Q(HRDATA_15_0), .clk(and_1_out), .clr(HRESET));  // open: en
  and and_1 (and_1_out, HSEL, HCLK, HWRITE);
  // Probe on 16'h7f
  Comparator #(.width(16), .mode("unsigned")) comparator_1 (.a(16'h7f), .b(HRDATA_15_0), .lt(HRESP));  // open: gt, eq

  assign HUPT_MAINDISPLAY = HRDATA_15_0[0];
  assign HUPT_SUBDISPLAY_1 = HRDATA_15_0[6];
  assign HUPT_SUBDISPLAY_2 = HRDATA_15_0[5];
  assign HUPT_SUBDISPLAY_3 = HRDATA_15_0[4];
  assign HUPT_SUBDISPLAY_4 = HRDATA_15_0[3];
  assign HUPT_SUBDISPLAY_5 = HRDATA_15_0[2];
  assign HUPT_SUBDISPLAY_6 = HRDATA_15_0[1];

  // Notes on the sheet:
  //   Slave controller rules update main display and sub-display
  //   The maximum value achievable by including all rules
endmodule

module Slave_SubDisplay (
  input  HWRITE,
  input  HSIZE,
  input  HCLK,
  input  HRESET,
  input  HSEL,
  input  [15:0] HWDATA_15_0,
  input  HUPT_1,
  input  [7:0] HADDR_7_0,
  input  HUPT_2,
  input  HUPT_3,
  input  HUPT_4,
  input  HUPT_5,
  input  HUPT_6,
  output [15:0] HRDATA_15_0,
  output HRESP,
  output [7:0] HLINE_1,
  output [7:0] HLINE_13,
  output [7:0] HLINE_25,
  output [7:0] HLINE_37,
  output [7:0] HLINE_2,
  output [7:0] HLINE_14,
  output [7:0] HLINEne_26,
  output [7:0] HLINE_38,
  output [7:0] HLINE_3,
  output [7:0] HLINE_15,
  output [7:0] HLINE_27,
  output [7:0] HLINE_39,
  output [7:0] HLINE_4,
  output [7:0] HLINE_16,
  output [7:0] HLINE_28,
  output [7:0] HLINE_40,
  output [7:0] HLINE_5,
  output [7:0] HLINE_17,
  output [7:0] HLINE_29,
  output [7:0] HLINE_41,
  output [7:0] HLINE_6,
  output [7:0] HLINE_18,
  output [7:0] HLINE_30,
  output [7:0] HLINE_42,
  output [7:0] HLINE_7,
  output [7:0] HLINE_19,
  output [7:0] HLINE_31,
  output [7:0] HLINE_43,
  output [7:0] HLINE_8,
  output [7:0] HLINE_20,
  output [7:0] HLINE_32,
  output [7:0] HLINE_44,
  output [7:0] HLINE_9,
  output [7:0] HLINE_21,
  output [7:0] HLINE_33,
  output [7:0] HLINE_45,
  output [7:0] HLINE_10,
  output [7:0] HLINE_22,
  output [7:0] HLINE_34,
  output [7:0] HLINE_46,
  output [7:0] HLINE_11,
  output [7:0] HLINE_23,
  output [7:0] HLINE_35,
  output [7:0] HLINE_47,
  output [7:0] HLINE_12,
  output [7:0] HLINE_24,
  output [7:0] HLINE_36,
  output [7:0] HLINE_48
);

  wire and_1_out, demultiplexer_1_out7, HSEL_L1, HSEL_L2, HSEL_L3, HSEL_L4, HSEL_L5, HSEL_L6, HSEL_L7,
       HSEL_L8, HSEL_L9, HSEL_L10, HSEL_L11, HSEL_L12, HSEL_L13, HSEL_L14, HSEL_L15, HSEL_L16, HSEL_L17,
       HSEL_L18, HSEL_L19, HSEL_L20, HSEL_L21, HSEL_L22, HSEL_L23, HSEL_L24, memoryupdater_1_hupdate,
       memoryupdater_2_hupdate, memoryupdater_3_hupdate, memoryupdater_4_hupdate, memoryupdater_5_hupdate,
       memoryupdater_6_hupdate, memoryupdater_7_hupdate, memoryupdater_8_hupdate, memoryupdater_9_hupdate,
       memoryupdater_10_hupdate, memoryupdater_11_hupdate, memoryupdater_12_hupdate,
       memoryupdater_13_hupdate, memoryupdater_14_hupdate, memoryupdater_15_hupdate,
       memoryupdater_16_hupdate, memoryupdater_17_hupdate, memoryupdater_18_hupdate,
       memoryupdater_19_hupdate, memoryupdater_20_hupdate, memoryupdater_21_hupdate,
       memoryupdater_22_hupdate, memoryupdater_23_hupdate, memoryupdater_24_hupdate;
  wire [7:0] register_1_q, register_2_q, register_3_q, register_4_q, register_5_q, register_6_q,
       register_7_q, register_8_q, register_9_q, register_10_q, register_11_q, register_12_q, register_25_q,
       register_26_q, register_27_q, register_28_q, register_29_q, register_30_q, register_31_q,
       register_33_q, register_35_q, register_38_q, register_39_q, register_41_q, register_49_q,
       register_50_q, register_51_q, register_52_q, register_53_q, register_54_q, register_55_q,
       register_56_q, register_57_q, register_58_q, register_59_q, register_60_q, register_73_q,
       register_74_q, register_75_q, register_76_q, register_77_q, register_78_q, register_79_q,
       register_81_q, register_83_q, register_85_q, register_87_q, register_89_q;

  Register register_1 (
    .D({HWDATA_15_0[8], HWDATA_15_0[9], HWDATA_15_0[10], HWDATA_15_0[11], HWDATA_15_0[12], HWDATA_15_0[13], HWDATA_15_0[14], HWDATA_15_0[15]}),
    .Q(register_1_q), .clk(HSEL_L1));  // open: en, clr
  Register register_2 (
    .D({HWDATA_15_0[0], HWDATA_15_0[1], HWDATA_15_0[2], HWDATA_15_0[3], HWDATA_15_0[4], HWDATA_15_0[5], HWDATA_15_0[6], HWDATA_15_0[7]}),
    .Q(register_2_q), .clk(HSEL_L1));  // open: en, clr
  MemoryUpdater memoryupdater_1 (.HSEL(HSEL_L1), .HUPT(HUPT_1), .HUPDATE(memoryupdater_1_hupdate));
  Register register_3 (
    .D({HWDATA_15_0[8], HWDATA_15_0[9], HWDATA_15_0[10], HWDATA_15_0[11], HWDATA_15_0[12], HWDATA_15_0[13], HWDATA_15_0[14], HWDATA_15_0[15]}),
    .Q(register_3_q), .clk(HSEL_L2));  // open: en, clr
  Register register_4 (
    .D({HWDATA_15_0[0], HWDATA_15_0[1], HWDATA_15_0[2], HWDATA_15_0[3], HWDATA_15_0[4], HWDATA_15_0[5], HWDATA_15_0[6], HWDATA_15_0[7]}),
    .Q(register_4_q), .clk(HSEL_L2));  // open: en, clr
  MemoryUpdater memoryupdater_2 (.HSEL(HSEL_L2), .HUPT(HUPT_1), .HUPDATE(memoryupdater_2_hupdate));
  Register register_5 (
    .D({HWDATA_15_0[8], HWDATA_15_0[9], HWDATA_15_0[10], HWDATA_15_0[11], HWDATA_15_0[12], HWDATA_15_0[13], HWDATA_15_0[14], HWDATA_15_0[15]}),
    .Q(register_5_q), .clk(HSEL_L3));  // open: en, clr
  Register register_6 (
    .D({HWDATA_15_0[0], HWDATA_15_0[1], HWDATA_15_0[2], HWDATA_15_0[3], HWDATA_15_0[4], HWDATA_15_0[5], HWDATA_15_0[6], HWDATA_15_0[7]}),
    .Q(register_6_q), .clk(HSEL_L3));  // open: en, clr
  MemoryUpdater memoryupdater_3 (.HSEL(HSEL_L3), .HUPT(HUPT_1), .HUPDATE(memoryupdater_3_hupdate));
  Register register_7 (
    .D({HWDATA_15_0[8], HWDATA_15_0[9], HWDATA_15_0[10], HWDATA_15_0[11], HWDATA_15_0[12], HWDATA_15_0[13], HWDATA_15_0[14], HWDATA_15_0[15]}),
    .Q(register_7_q), .clk(HSEL_L4));  // open: en, clr
  Register register_8 (
    .D({HWDATA_15_0[0], HWDATA_15_0[1], HWDATA_15_0[2], HWDATA_15_0[3], HWDATA_15_0[4], HWDATA_15_0[5], HWDATA_15_0[6], HWDATA_15_0[7]}),
    .Q(register_8_q), .clk(HSEL_L4));  // open: en, clr
  MemoryUpdater memoryupdater_4 (.HSEL(HSEL_L4), .HUPT(HUPT_1), .HUPDATE(memoryupdater_4_hupdate));
  Register register_9 (
    .D({HWDATA_15_0[8], HWDATA_15_0[9], HWDATA_15_0[10], HWDATA_15_0[11], HWDATA_15_0[12], HWDATA_15_0[13], HWDATA_15_0[14], HWDATA_15_0[15]}),
    .Q(register_9_q), .clk(HSEL_L5));  // open: en, clr
  Register register_10 (
    .D({HWDATA_15_0[0], HWDATA_15_0[1], HWDATA_15_0[2], HWDATA_15_0[3], HWDATA_15_0[4], HWDATA_15_0[5], HWDATA_15_0[6], HWDATA_15_0[7]}),
    .Q(register_10_q), .clk(HSEL_L5));  // open: en, clr
  MemoryUpdater memoryupdater_5 (.HSEL(HSEL_L5), .HUPT(HUPT_2), .HUPDATE(memoryupdater_5_hupdate));
  Register register_11 (
    .D({HWDATA_15_0[8], HWDATA_15_0[9], HWDATA_15_0[10], HWDATA_15_0[11], HWDATA_15_0[12], HWDATA_15_0[13], HWDATA_15_0[14], HWDATA_15_0[15]}),
    .Q(register_11_q), .clk(HSEL_L6));  // open: en, clr
  Register register_12 (
    .D({HWDATA_15_0[0], HWDATA_15_0[1], HWDATA_15_0[2], HWDATA_15_0[3], HWDATA_15_0[4], HWDATA_15_0[5], HWDATA_15_0[6], HWDATA_15_0[7]}),
    .Q(register_12_q), .clk(HSEL_L6));  // open: en, clr
  MemoryUpdater memoryupdater_6 (.HSEL(HSEL_L6), .HUPT(HUPT_2), .HUPDATE(memoryupdater_6_hupdate));
  Register register_13 (.D(register_1_q), .Q(HLINE_1), .clk(memoryupdater_1_hupdate));  // open: en, clr
  Register register_14 (.D(register_2_q), .Q(HLINE_2), .clk(memoryupdater_1_hupdate));  // open: en, clr
  Register register_15 (.D(register_3_q), .Q(HLINE_3), .clk(memoryupdater_2_hupdate));  // open: en, clr
  Register register_16 (.D(register_4_q), .Q(HLINE_4), .clk(memoryupdater_2_hupdate));  // open: en, clr
  Register register_17 (.D(register_5_q), .Q(HLINE_5), .clk(memoryupdater_3_hupdate));  // open: en, clr
  Register register_18 (.D(register_6_q), .Q(HLINE_6), .clk(memoryupdater_3_hupdate));  // open: en, clr
  Register register_19 (.D(register_7_q), .Q(HLINE_7), .clk(memoryupdater_4_hupdate));  // open: en, clr
  Register register_20 (.D(register_8_q), .Q(HLINE_8), .clk(memoryupdater_4_hupdate));  // open: en, clr
  Register register_21 (.D(register_9_q), .Q(HLINE_9), .clk(memoryupdater_5_hupdate));  // open: en, clr
  Register register_22 (.D(register_10_q), .Q(HLINE_10), .clk(memoryupdater_5_hupdate));  // open: en, clr
  Register register_23 (.D(register_11_q), .Q(HLINE_11), .clk(memoryupdater_6_hupdate));  // open: en, clr
  Register register_24 (.D(register_12_q), .Q(HLINE_12), .clk(memoryupdater_6_hupdate));  // open: en, clr
  and and_1 (and_1_out, HWRITE, HCLK, HSEL);
  Demultiplexer #(.select(5)) demultiplexer_1 (
    .out7(demultiplexer_1_out7), .out8(HSEL_L1), .out9(HSEL_L2), .out10(HSEL_L3), .out11(HSEL_L4),
    .out12(HSEL_L5), .out13(HSEL_L6), .out14(HSEL_L7), .out15(HSEL_L8), .out16(HSEL_L9), .out17(HSEL_L10),
    .out18(HSEL_L11), .out19(HSEL_L12), .out20(HSEL_L13), .out21(HSEL_L14), .out22(HSEL_L15),
    .out23(HSEL_L16), .out24(HSEL_L17), .out25(HSEL_L18), .out26(HSEL_L19), .out27(HSEL_L20),
    .out28(HSEL_L21), .out29(HSEL_L22), .out30(HSEL_L23), .out31(HSEL_L24), .in(and_1_out),
    .sel(HADDR_7_0[5:1]));  // open: out0, out1, out2, out3, out4, out5, out6, en
  Register register_25 (
    .D({HWDATA_15_0[0], HWDATA_15_0[1], HWDATA_15_0[2], HWDATA_15_0[3], HWDATA_15_0[4], HWDATA_15_0[5], HWDATA_15_0[6], HWDATA_15_0[7]}),
    .Q(register_25_q), .clk(HSEL_L7));  // open: en, clr
  Register register_26 (
    .D({HWDATA_15_0[0], HWDATA_15_0[1], HWDATA_15_0[2], HWDATA_15_0[3], HWDATA_15_0[4], HWDATA_15_0[5], HWDATA_15_0[6], HWDATA_15_0[7]}),
    .Q(register_26_q), .clk(HSEL_L8));  // open: en, clr
  Register register_27 (
    .D({HWDATA_15_0[0], HWDATA_15_0[1], HWDATA_15_0[2], HWDATA_15_0[3], HWDATA_15_0[4], HWDATA_15_0[5], HWDATA_15_0[6], HWDATA_15_0[7]}),
    .Q(register_27_q), .clk(HSEL_L9));  // open: en, clr
  Register register_28 (
    .D({HWDATA_15_0[0], HWDATA_15_0[1], HWDATA_15_0[2], HWDATA_15_0[3], HWDATA_15_0[4], HWDATA_15_0[5], HWDATA_15_0[6], HWDATA_15_0[7]}),
    .Q(register_28_q), .clk(HSEL_L10));  // open: en, clr
  Register register_29 (
    .D({HWDATA_15_0[0], HWDATA_15_0[1], HWDATA_15_0[2], HWDATA_15_0[3], HWDATA_15_0[4], HWDATA_15_0[5], HWDATA_15_0[6], HWDATA_15_0[7]}),
    .Q(register_29_q), .clk(HSEL_L11));  // open: en, clr
  Register register_30 (
    .D({HWDATA_15_0[0], HWDATA_15_0[1], HWDATA_15_0[2], HWDATA_15_0[3], HWDATA_15_0[4], HWDATA_15_0[5], HWDATA_15_0[6], HWDATA_15_0[7]}),
    .Q(register_30_q), .clk(HSEL_L12));  // open: en, clr
  Register register_31 (
    .D({HWDATA_15_0[8], HWDATA_15_0[9], HWDATA_15_0[10], HWDATA_15_0[11], HWDATA_15_0[12], HWDATA_15_0[13], HWDATA_15_0[14], HWDATA_15_0[15]}),
    .Q(register_31_q), .clk(HSEL_L7));  // open: en, clr
  Register register_32 (.D(register_31_q), .Q(HLINE_13), .clk(memoryupdater_7_hupdate));  // open: en, clr
  MemoryUpdater memoryupdater_7 (.HSEL(HSEL_L7), .HUPT(HUPT_2), .HUPDATE(memoryupdater_7_hupdate));
  Register register_33 (
    .D({HWDATA_15_0[8], HWDATA_15_0[9], HWDATA_15_0[10], HWDATA_15_0[11], HWDATA_15_0[12], HWDATA_15_0[13], HWDATA_15_0[14], HWDATA_15_0[15]}),
    .Q(register_33_q), .clk(HSEL_L8));  // open: en, clr
  Register register_34 (.D(register_33_q), .Q(HLINE_15), .clk(memoryupdater_8_hupdate));  // open: en, clr
  MemoryUpdater memoryupdater_8 (.HSEL(HSEL_L8), .HUPT(HUPT_2), .HUPDATE(memoryupdater_8_hupdate));
  Register register_35 (
    .D({HWDATA_15_0[8], HWDATA_15_0[9], HWDATA_15_0[10], HWDATA_15_0[11], HWDATA_15_0[12], HWDATA_15_0[13], HWDATA_15_0[14], HWDATA_15_0[15]}),
    .Q(register_35_q), .clk(HSEL_L9));  // open: en, clr
  Register register_36 (.D(register_35_q), .Q(HLINE_17), .clk(memoryupdater_9_hupdate));  // open: en, clr
  MemoryUpdater memoryupdater_9 (.HSEL(HSEL_L9), .HUPT(HUPT_3), .HUPDATE(memoryupdater_9_hupdate));
  Register register_37 (.D(register_38_q), .Q(HLINE_19), .clk(memoryupdater_10_hupdate));  // open: en, clr
  Register register_38 (
    .D({HWDATA_15_0[8], HWDATA_15_0[9], HWDATA_15_0[10], HWDATA_15_0[11], HWDATA_15_0[12], HWDATA_15_0[13], HWDATA_15_0[14], HWDATA_15_0[15]}),
    .Q(register_38_q), .clk(HSEL_L10));  // open: en, clr
  MemoryUpdater memoryupdater_10 (.HSEL(HSEL_L10), .HUPT(HUPT_3), .HUPDATE(memoryupdater_10_hupdate));
  Register register_39 (
    .D({HWDATA_15_0[8], HWDATA_15_0[9], HWDATA_15_0[10], HWDATA_15_0[11], HWDATA_15_0[12], HWDATA_15_0[13], HWDATA_15_0[14], HWDATA_15_0[15]}),
    .Q(register_39_q), .clk(HSEL_L11));  // open: en, clr
  Register register_40 (.D(register_39_q), .Q(HLINE_21), .clk(memoryupdater_11_hupdate));  // open: en, clr
  MemoryUpdater memoryupdater_11 (.HSEL(HSEL_L11), .HUPT(HUPT_3), .HUPDATE(memoryupdater_11_hupdate));
  Register register_41 (
    .D({HWDATA_15_0[8], HWDATA_15_0[9], HWDATA_15_0[10], HWDATA_15_0[11], HWDATA_15_0[12], HWDATA_15_0[13], HWDATA_15_0[14], HWDATA_15_0[15]}),
    .Q(register_41_q), .clk(HSEL_L12));  // open: en, clr
  Register register_42 (.D(register_41_q), .Q(HLINE_23), .clk(memoryupdater_12_hupdate));  // open: en, clr
  MemoryUpdater memoryupdater_12 (.HSEL(HSEL_L12), .HUPT(HUPT_3), .HUPDATE(memoryupdater_12_hupdate));
  Register register_43 (.D(register_25_q), .Q(HLINE_14), .clk(memoryupdater_7_hupdate));  // open: en, clr
  Register register_44 (.D(register_26_q), .Q(HLINE_16), .clk(memoryupdater_8_hupdate));  // open: en, clr
  Register register_45 (.D(register_27_q), .Q(HLINE_18), .clk(memoryupdater_9_hupdate));  // open: en, clr
  Register register_46 (.D(register_28_q), .Q(HLINE_20), .clk(memoryupdater_10_hupdate));  // open: en, clr
  Register register_47 (.D(register_29_q), .Q(HLINE_22), .clk(memoryupdater_11_hupdate));  // open: en, clr
  Register register_48 (.D(register_30_q), .Q(HLINE_24), .clk(memoryupdater_12_hupdate));  // open: en, clr
  Pull_Resistor pull_resistor_1 (.node(HRDATA_15_0));
  Pull_Resistor pull_resistor_2 (.node(HRESP));
  Register register_49 (
    .D({HWDATA_15_0[8], HWDATA_15_0[9], HWDATA_15_0[10], HWDATA_15_0[11], HWDATA_15_0[12], HWDATA_15_0[13], HWDATA_15_0[14], HWDATA_15_0[15]}),
    .Q(register_49_q), .clk(HSEL_L13));  // open: en, clr
  Register register_50 (
    .D({HWDATA_15_0[0], HWDATA_15_0[1], HWDATA_15_0[2], HWDATA_15_0[3], HWDATA_15_0[4], HWDATA_15_0[5], HWDATA_15_0[6], HWDATA_15_0[7]}),
    .Q(register_50_q), .clk(HSEL_L13));  // open: en, clr
  MemoryUpdater memoryupdater_13 (.HSEL(HSEL_L13), .HUPT(HUPT_4), .HUPDATE(memoryupdater_13_hupdate));
  Register register_51 (
    .D({HWDATA_15_0[8], HWDATA_15_0[9], HWDATA_15_0[10], HWDATA_15_0[11], HWDATA_15_0[12], HWDATA_15_0[13], HWDATA_15_0[14], HWDATA_15_0[15]}),
    .Q(register_51_q), .clk(HSEL_L14));  // open: en, clr
  Register register_52 (
    .D({HWDATA_15_0[0], HWDATA_15_0[1], HWDATA_15_0[2], HWDATA_15_0[3], HWDATA_15_0[4], HWDATA_15_0[5], HWDATA_15_0[6], HWDATA_15_0[7]}),
    .Q(register_52_q), .clk(HSEL_L14));  // open: en, clr
  MemoryUpdater memoryupdater_14 (.HSEL(HSEL_L14), .HUPT(HUPT_4), .HUPDATE(memoryupdater_14_hupdate));
  Register register_53 (
    .D({HWDATA_15_0[8], HWDATA_15_0[9], HWDATA_15_0[10], HWDATA_15_0[11], HWDATA_15_0[12], HWDATA_15_0[13], HWDATA_15_0[14], HWDATA_15_0[15]}),
    .Q(register_53_q), .clk(HSEL_L15));  // open: en, clr
  Register register_54 (
    .D({HWDATA_15_0[0], HWDATA_15_0[1], HWDATA_15_0[2], HWDATA_15_0[3], HWDATA_15_0[4], HWDATA_15_0[5], HWDATA_15_0[6], HWDATA_15_0[7]}),
    .Q(register_54_q), .clk(HSEL_L15));  // open: en, clr
  MemoryUpdater memoryupdater_15 (.HSEL(HSEL_L15), .HUPT(HUPT_4), .HUPDATE(memoryupdater_15_hupdate));
  Register register_55 (
    .D({HWDATA_15_0[8], HWDATA_15_0[9], HWDATA_15_0[10], HWDATA_15_0[11], HWDATA_15_0[12], HWDATA_15_0[13], HWDATA_15_0[14], HWDATA_15_0[15]}),
    .Q(register_55_q), .clk(HSEL_L16));  // open: en, clr
  Register register_56 (
    .D({HWDATA_15_0[0], HWDATA_15_0[1], HWDATA_15_0[2], HWDATA_15_0[3], HWDATA_15_0[4], HWDATA_15_0[5], HWDATA_15_0[6], HWDATA_15_0[7]}),
    .Q(register_56_q), .clk(HSEL_L16));  // open: en, clr
  MemoryUpdater memoryupdater_16 (.HSEL(HSEL_L16), .HUPT(HUPT_4), .HUPDATE(memoryupdater_16_hupdate));
  Register register_57 (
    .D({HWDATA_15_0[8], HWDATA_15_0[9], HWDATA_15_0[10], HWDATA_15_0[11], HWDATA_15_0[12], HWDATA_15_0[13], HWDATA_15_0[14], HWDATA_15_0[15]}),
    .Q(register_57_q), .clk(HSEL_L17));  // open: en, clr
  Register register_58 (
    .D({HWDATA_15_0[0], HWDATA_15_0[1], HWDATA_15_0[2], HWDATA_15_0[3], HWDATA_15_0[4], HWDATA_15_0[5], HWDATA_15_0[6], HWDATA_15_0[7]}),
    .Q(register_58_q), .clk(HSEL_L17));  // open: en, clr
  MemoryUpdater memoryupdater_17 (.HSEL(HSEL_L17), .HUPT(HUPT_5), .HUPDATE(memoryupdater_17_hupdate));
  Register register_59 (
    .D({HWDATA_15_0[8], HWDATA_15_0[9], HWDATA_15_0[10], HWDATA_15_0[11], HWDATA_15_0[12], HWDATA_15_0[13], HWDATA_15_0[14], HWDATA_15_0[15]}),
    .Q(register_59_q), .clk(HSEL_L18));  // open: en, clr
  Register register_60 (
    .D({HWDATA_15_0[0], HWDATA_15_0[1], HWDATA_15_0[2], HWDATA_15_0[3], HWDATA_15_0[4], HWDATA_15_0[5], HWDATA_15_0[6], HWDATA_15_0[7]}),
    .Q(register_60_q), .clk(HSEL_L18));  // open: en, clr
  MemoryUpdater memoryupdater_18 (.HSEL(HSEL_L18), .HUPT(HUPT_5), .HUPDATE(memoryupdater_18_hupdate));
  Register register_61 (.D(register_49_q), .Q(HLINE_25), .clk(memoryupdater_13_hupdate));  // open: en, clr
  Register register_62 (.D(register_50_q), .Q(HLINEne_26), .clk(memoryupdater_13_hupdate));  // open: en, clr
  Register register_63 (.D(register_51_q), .Q(HLINE_27), .clk(memoryupdater_14_hupdate));  // open: en, clr
  Register register_64 (.D(register_52_q), .Q(HLINE_28), .clk(memoryupdater_14_hupdate));  // open: en, clr
  Register register_65 (.D(register_53_q), .Q(HLINE_29), .clk(memoryupdater_15_hupdate));  // open: en, clr
  Register register_66 (.D(register_54_q), .Q(HLINE_30), .clk(memoryupdater_15_hupdate));  // open: en, clr
  Register register_67 (.D(register_55_q), .Q(HLINE_31), .clk(memoryupdater_16_hupdate));  // open: en, clr
  Register register_68 (.D(register_56_q), .Q(HLINE_32), .clk(memoryupdater_16_hupdate));  // open: en, clr
  Register register_69 (.D(register_57_q), .Q(HLINE_33), .clk(memoryupdater_17_hupdate));  // open: en, clr
  Register register_70 (.D(register_58_q), .Q(HLINE_34), .clk(memoryupdater_17_hupdate));  // open: en, clr
  Register register_71 (.D(register_59_q), .Q(HLINE_35), .clk(memoryupdater_18_hupdate));  // open: en, clr
  Register register_72 (.D(register_60_q), .Q(HLINE_36), .clk(memoryupdater_18_hupdate));  // open: en, clr
  Register register_73 (
    .D({HWDATA_15_0[0], HWDATA_15_0[1], HWDATA_15_0[2], HWDATA_15_0[3], HWDATA_15_0[4], HWDATA_15_0[5], HWDATA_15_0[6], HWDATA_15_0[7]}),
    .Q(register_73_q), .clk(HSEL_L19));  // open: en, clr
  Register register_74 (
    .D({HWDATA_15_0[0], HWDATA_15_0[1], HWDATA_15_0[2], HWDATA_15_0[3], HWDATA_15_0[4], HWDATA_15_0[5], HWDATA_15_0[6], HWDATA_15_0[7]}),
    .Q(register_74_q), .clk(HSEL_L20));  // open: en, clr
  Register register_75 (
    .D({HWDATA_15_0[0], HWDATA_15_0[1], HWDATA_15_0[2], HWDATA_15_0[3], HWDATA_15_0[4], HWDATA_15_0[5], HWDATA_15_0[6], HWDATA_15_0[7]}),
    .Q(register_75_q), .clk(HSEL_L21));  // open: en, clr
  Register register_76 (
    .D({HWDATA_15_0[0], HWDATA_15_0[1], HWDATA_15_0[2], HWDATA_15_0[3], HWDATA_15_0[4], HWDATA_15_0[5], HWDATA_15_0[6], HWDATA_15_0[7]}),
    .Q(register_76_q), .clk(HSEL_L22));  // open: en, clr
  Register register_77 (
    .D({HWDATA_15_0[0], HWDATA_15_0[1], HWDATA_15_0[2], HWDATA_15_0[3], HWDATA_15_0[4], HWDATA_15_0[5], HWDATA_15_0[6], HWDATA_15_0[7]}),
    .Q(register_77_q), .clk(HSEL_L23));  // open: en, clr
  Register register_78 (
    .D({HWDATA_15_0[0], HWDATA_15_0[1], HWDATA_15_0[2], HWDATA_15_0[3], HWDATA_15_0[4], HWDATA_15_0[5], HWDATA_15_0[6], HWDATA_15_0[7]}),
    .Q(register_78_q), .clk(HSEL_L24));  // open: en, clr
  Register register_79 (
    .D({HWDATA_15_0[8], HWDATA_15_0[9], HWDATA_15_0[10], HWDATA_15_0[11], HWDATA_15_0[12], HWDATA_15_0[13], HWDATA_15_0[14], HWDATA_15_0[15]}),
    .Q(register_79_q), .clk(HSEL_L19));  // open: en, clr
  Register register_80 (.D(register_79_q), .Q(HLINE_37), .clk(memoryupdater_19_hupdate));  // open: en, clr
  MemoryUpdater memoryupdater_19 (.HSEL(HSEL_L19), .HUPT(HUPT_5), .HUPDATE(memoryupdater_19_hupdate));
  Register register_81 (
    .D({HWDATA_15_0[8], HWDATA_15_0[9], HWDATA_15_0[10], HWDATA_15_0[11], HWDATA_15_0[12], HWDATA_15_0[13], HWDATA_15_0[14], HWDATA_15_0[15]}),
    .Q(register_81_q), .clk(HSEL_L20));  // open: en, clr
  Register register_82 (.D(register_81_q), .Q(HLINE_39), .clk(memoryupdater_20_hupdate));  // open: en, clr
  MemoryUpdater memoryupdater_20 (.HSEL(HSEL_L20), .HUPT(HUPT_5), .HUPDATE(memoryupdater_20_hupdate));
  Register register_83 (
    .D({HWDATA_15_0[8], HWDATA_15_0[9], HWDATA_15_0[10], HWDATA_15_0[11], HWDATA_15_0[12], HWDATA_15_0[13], HWDATA_15_0[14], HWDATA_15_0[15]}),
    .Q(register_83_q), .clk(HSEL_L21));  // open: en, clr
  Register register_84 (.D(register_83_q), .Q(HLINE_41), .clk(memoryupdater_21_hupdate));  // open: en, clr
  MemoryUpdater memoryupdater_21 (.HSEL(HSEL_L21), .HUPT(HUPT_6), .HUPDATE(memoryupdater_21_hupdate));
  Register register_85 (
    .D({HWDATA_15_0[8], HWDATA_15_0[9], HWDATA_15_0[10], HWDATA_15_0[11], HWDATA_15_0[12], HWDATA_15_0[13], HWDATA_15_0[14], HWDATA_15_0[15]}),
    .Q(register_85_q), .clk(HSEL_L22));  // open: en, clr
  Register register_86 (.D(register_85_q), .Q(HLINE_43), .clk(memoryupdater_22_hupdate));  // open: en, clr
  MemoryUpdater memoryupdater_22 (.HSEL(HSEL_L22), .HUPT(HUPT_6), .HUPDATE(memoryupdater_22_hupdate));
  Register register_87 (
    .D({HWDATA_15_0[8], HWDATA_15_0[9], HWDATA_15_0[10], HWDATA_15_0[11], HWDATA_15_0[12], HWDATA_15_0[13], HWDATA_15_0[14], HWDATA_15_0[15]}),
    .Q(register_87_q), .clk(HSEL_L23));  // open: en, clr
  Register register_88 (.D(register_87_q), .Q(HLINE_45), .clk(memoryupdater_23_hupdate));  // open: en, clr
  MemoryUpdater memoryupdater_23 (.HSEL(HSEL_L23), .HUPT(HUPT_6), .HUPDATE(memoryupdater_23_hupdate));
  Register register_89 (
    .D({HWDATA_15_0[8], HWDATA_15_0[9], HWDATA_15_0[10], HWDATA_15_0[11], HWDATA_15_0[12], HWDATA_15_0[13], HWDATA_15_0[14], HWDATA_15_0[15]}),
    .Q(register_89_q), .clk(HSEL_L24));  // open: en, clr
  Register register_90 (.D(register_89_q), .Q(HLINE_47), .clk(memoryupdater_24_hupdate));  // open: en, clr
  MemoryUpdater memoryupdater_24 (.HSEL(HSEL_L24), .HUPT(HUPT_6), .HUPDATE(memoryupdater_24_hupdate));
  Register register_91 (.D(register_73_q), .Q(HLINE_38), .clk(memoryupdater_19_hupdate));  // open: en, clr
  Register register_92 (.D(register_74_q), .Q(HLINE_40), .clk(memoryupdater_20_hupdate));  // open: en, clr
  Register register_93 (.D(register_75_q), .Q(HLINE_42), .clk(memoryupdater_21_hupdate));  // open: en, clr
  Register register_94 (.D(register_76_q), .Q(HLINE_44), .clk(memoryupdater_22_hupdate));  // open: en, clr
  Register register_95 (.D(register_77_q), .Q(HLINE_46), .clk(memoryupdater_23_hupdate));  // open: en, clr
  Register register_96 (.D(register_78_q), .Q(HLINE_48), .clk(memoryupdater_24_hupdate));  // open: en, clr

  // Notes on the sheet:
  //   Distribution into 24 blocks with two 8-bit lines in each
  //   Slave sub-display showing the letters of the gallows hidden word
  //   2-nd line
  //   1-st line
endmodule

module Slave_MainDisplay (
  input  HWRITE,
  input  HCLK,
  input  HSEL,
  input  [7:0] HADDR_7_0,
  input  [15:0] HWDATA_15_0,
  input  HRESET,
  input  HSIZE,
  input  HUPT,
  output [15:0] HRDATA_15_0,
  output HRESP,
  output [31:0] line_1,
  output [31:0] line_2,
  output [31:0] line_3,
  output [31:0] line_4,
  output [31:0] line_5,
  output [31:0] line_6,
  output [31:0] line_7,
  output [31:0] line_8,
  output [31:0] line_9,
  output [31:0] line_10,
  output [31:0] line_11,
  output [31:0] line_12,
  output [31:0] line_13,
  output [31:0] line_14,
  output [31:0] line_15,
  output [31:0] line_16,
  output [31:0] line_17,
  output [31:0] line_18,
  output [31:0] line_19,
  output [31:0] line_20,
  output [31:0] line_21,
  output [31:0] line_22,
  output [31:0] line_23,
  output [31:0] line_24,
  output [31:0] line_25,
  output [31:0] line_26,
  output [31:0] line_27,
  output [31:0] line_28,
  output [31:0] line_29,
  output [31:0] line_30,
  output [31:0] line_31,
  output [31:0] line_32
);

  wire and_1_out, and_2_out, and_3_out, counter_1_carry, demultiplexer_1_out0, demultiplexer_1_out1, HSEL_1,
       HSEL_2, HSEL_3, HSEL_4, HSEL_5, HSEL_6, HSEL_7, HSEL_8, HSEL_9, HSEL_10, HSEL_11, HSEL_12, HSEL_13,
       HSEL_14, HSEL_15, HSEL_16, HSEL_17, HSEL_18, HSEL_19, HSEL_20, HSEL_21, HSEL_22, HSEL_23, HSEL_24,
       HSEL_25, HSEL_26, HSEL_27, HSEL_28, HSEL_29, HSEL_30, HSEL_31, HSEL_32, memoryupdater_1_hupdate,
       memoryupdater_2_hupdate, memoryupdater_3_hupdate, memoryupdater_4_hupdate, memoryupdater_5_hupdate,
       memoryupdater_6_hupdate, memoryupdater_7_hupdate, memoryupdater_8_hupdate, memoryupdater_9_hupdate,
       memoryupdater_10_hupdate, memoryupdater_11_hupdate, memoryupdater_12_hupdate,
       memoryupdater_13_hupdate, memoryupdater_14_hupdate, memoryupdater_15_hupdate,
       memoryupdater_16_hupdate, memoryupdater_17_hupdate, memoryupdater_18_hupdate,
       memoryupdater_19_hupdate, memoryupdater_20_hupdate, memoryupdater_21_hupdate,
       memoryupdater_22_hupdate, memoryupdater_23_hupdate, memoryupdater_24_hupdate,
       memoryupdater_25_hupdate, memoryupdater_26_hupdate, memoryupdater_27_hupdate,
       memoryupdater_28_hupdate, memoryupdater_29_hupdate, memoryupdater_30_hupdate,
       memoryupdater_31_hupdate, memoryupdater_32_hupdate, not_1_out, not_2_out, not_3_out, not_4_out;
  wire [15:0] register_25_q, register_26_q;
  wire [31:0] register_1_q, register_2_q, register_3_q, register_4_q, register_5_q, register_6_q,
       register_7_q, register_8_q, register_17_q, register_18_q, register_19_q, register_20_q, register_21_q,
       register_22_q, register_23_q, register_24_q, register_35_q, register_36_q, register_37_q,
       register_38_q, register_39_q, register_40_q, register_41_q, register_42_q, register_51_q,
       register_52_q, register_53_q, register_54_q, register_55_q, register_56_q, register_57_q,
       register_58_q;

  Register #(.width(32)) register_1 (
    .D({register_25_q, register_26_q}), .Q(register_1_q), .clk(HSEL_1));  // open: en, clr
  MemoryUpdater memoryupdater_1 (.HSEL(HSEL_1), .HUPT(HUPT), .HUPDATE(memoryupdater_1_hupdate));
  Register #(.width(32)) register_2 (
    .D({register_25_q, register_26_q}), .Q(register_2_q), .clk(HSEL_5));  // open: en, clr
  MemoryUpdater memoryupdater_2 (.HSEL(HSEL_5), .HUPT(HUPT), .HUPDATE(memoryupdater_2_hupdate));
  Register #(.width(32)) register_3 (
    .D({register_25_q, register_26_q}), .Q(register_3_q), .clk(HSEL_9));  // open: en, clr
  MemoryUpdater memoryupdater_3 (.HSEL(HSEL_9), .HUPT(HUPT), .HUPDATE(memoryupdater_3_hupdate));
  Register #(.width(32)) register_4 (
    .D({register_25_q, register_26_q}), .Q(register_4_q), .clk(HSEL_13));  // open: en, clr
  MemoryUpdater memoryupdater_4 (.HSEL(HSEL_13), .HUPT(HUPT), .HUPDATE(memoryupdater_4_hupdate));
  Register #(.width(32)) register_5 (
    .D({register_25_q, register_26_q}), .Q(register_5_q), .clk(HSEL_17));  // open: en, clr
  MemoryUpdater memoryupdater_5 (.HSEL(HSEL_17), .HUPT(HUPT), .HUPDATE(memoryupdater_5_hupdate));
  Register #(.width(32)) register_6 (
    .D({register_25_q, register_26_q}), .Q(register_6_q), .clk(HSEL_21));  // open: en, clr
  MemoryUpdater memoryupdater_6 (.HSEL(HSEL_21), .HUPT(HUPT), .HUPDATE(memoryupdater_6_hupdate));
  Register #(.width(32)) register_7 (
    .D({register_25_q, register_26_q}), .Q(register_7_q), .clk(HSEL_25));  // open: en, clr
  MemoryUpdater memoryupdater_7 (.HSEL(HSEL_25), .HUPT(HUPT), .HUPDATE(memoryupdater_7_hupdate));
  Register #(.width(32)) register_8 (
    .D({register_25_q, register_26_q}), .Q(register_8_q), .clk(HSEL_29));  // open: en, clr
  MemoryUpdater memoryupdater_8 (.HSEL(HSEL_29), .HUPT(HUPT), .HUPDATE(memoryupdater_8_hupdate));
  Register #(.width(32)) register_9 (.D(register_1_q), .Q(line_1), .clk(memoryupdater_1_hupdate));  // open: en, clr
  Register #(.width(32)) register_10 (.D(register_2_q), .Q(line_5), .clk(memoryupdater_2_hupdate));  // open: en, clr
  Register #(.width(32)) register_11 (.D(register_3_q), .Q(line_9), .clk(memoryupdater_3_hupdate));  // open: en, clr
  Register #(.width(32)) register_12 (.D(register_4_q), .Q(line_13), .clk(memoryupdater_4_hupdate));  // open: en, clr
  Register #(.width(32)) register_13 (.D(register_5_q), .Q(line_17), .clk(memoryupdater_5_hupdate));  // open: en, clr
  Register #(.width(32)) register_14 (.D(register_6_q), .Q(line_21), .clk(memoryupdater_6_hupdate));  // open: en, clr
  Register #(.width(32)) register_15 (.D(register_7_q), .Q(line_25), .clk(memoryupdater_7_hupdate));  // open: en, clr
  Register #(.width(32)) register_16 (.D(register_8_q), .Q(line_29), .clk(memoryupdater_8_hupdate));  // open: en, clr
  and and_1 (and_1_out, HWRITE, HCLK, HSEL);
  Demultiplexer demultiplexer_1 (
    .out0(demultiplexer_1_out0), .out1(demultiplexer_1_out1), .in(and_1_out), .sel(HADDR_7_0[1]));  // open: en
  Pull_Resistor pull_resistor_1 (.node(HRDATA_15_0));
  Pull_Resistor pull_resistor_2 (.node(HRESP));
  Counter #(.width(2), .max('h2)) counter_1 (
    .carry(counter_1_carry), .clk(and_1_out), .clr(and_2_out));  // open: load, D, count, Q
  and and_2 (and_2_out, counter_1_carry, ~and_1_out);  // AND_Gate
  Register #(.width(32)) register_17 (
    .D({register_25_q, register_26_q}), .Q(register_17_q), .clk(HSEL_2));  // open: en, clr
  MemoryUpdater memoryupdater_9 (.HSEL(HSEL_2), .HUPT(HUPT), .HUPDATE(memoryupdater_9_hupdate));
  Register #(.width(32)) register_18 (
    .D({register_25_q, register_26_q}), .Q(register_18_q), .clk(HSEL_6));  // open: en, clr
  MemoryUpdater memoryupdater_10 (.HSEL(HSEL_6), .HUPT(HUPT), .HUPDATE(memoryupdater_10_hupdate));
  Register #(.width(32)) register_19 (
    .D({register_25_q, register_26_q}), .Q(register_19_q), .clk(HSEL_10));  // open: en, clr
  MemoryUpdater memoryupdater_11 (.HSEL(HSEL_10), .HUPT(HUPT), .HUPDATE(memoryupdater_11_hupdate));
  Register #(.width(32)) register_20 (
    .D({register_25_q, register_26_q}), .Q(register_20_q), .clk(HSEL_14));  // open: en, clr
  MemoryUpdater memoryupdater_12 (.HSEL(HSEL_14), .HUPT(HUPT), .HUPDATE(memoryupdater_12_hupdate));
  Register #(.width(32)) register_21 (
    .D({register_25_q, register_26_q}), .Q(register_21_q), .clk(HSEL_18));  // open: en, clr
  MemoryUpdater memoryupdater_13 (.HSEL(HSEL_18), .HUPT(HUPT), .HUPDATE(memoryupdater_13_hupdate));
  Register #(.width(32)) register_22 (
    .D({register_25_q, register_26_q}), .Q(register_22_q), .clk(HSEL_22));  // open: en, clr
  MemoryUpdater memoryupdater_14 (.HSEL(HSEL_22), .HUPT(HUPT), .HUPDATE(memoryupdater_14_hupdate));
  Register #(.width(32)) register_23 (
    .D({register_25_q, register_26_q}), .Q(register_23_q), .clk(HSEL_26));  // open: en, clr
  MemoryUpdater memoryupdater_15 (.HSEL(HSEL_26), .HUPT(HUPT), .HUPDATE(memoryupdater_15_hupdate));
  Register #(.width(32)) register_24 (
    .D({register_25_q, register_26_q}), .Q(register_24_q), .clk(HSEL_30));  // open: en, clr
  MemoryUpdater memoryupdater_16 (.HSEL(HSEL_30), .HUPT(HUPT), .HUPDATE(memoryupdater_16_hupdate));
  Pull_Resistor pull_resistor_3 (.node(counter_1_carry));
  and and_3 (and_3_out, counter_1_carry, and_1_out);
  Register #(.width(16)) register_25 (.D(HWDATA_15_0), .Q(register_25_q), .clk(demultiplexer_1_out0));  // open: en, clr
  Register #(.width(16)) register_26 (.D(HWDATA_15_0), .Q(register_26_q), .clk(demultiplexer_1_out1));  // open: en, clr
  Register #(.width(32)) register_27 (.D(register_17_q), .Q(line_2), .clk(memoryupdater_9_hupdate));  // open: en, clr
  Register #(.width(32)) register_28 (.D(register_18_q), .Q(line_6), .clk(memoryupdater_10_hupdate));  // open: en, clr
  Register #(.width(32)) register_29 (.D(register_19_q), .Q(line_10), .clk(memoryupdater_11_hupdate));  // open: en, clr
  Register #(.width(32)) register_30 (.D(register_20_q), .Q(line_14), .clk(memoryupdater_12_hupdate));  // open: en, clr
  Register #(.width(32)) register_31 (.D(register_21_q), .Q(line_18), .clk(memoryupdater_13_hupdate));  // open: en, clr
  Register #(.width(32)) register_32 (.D(register_22_q), .Q(line_22), .clk(memoryupdater_14_hupdate));  // open: en, clr
  Register #(.width(32)) register_33 (.D(register_23_q), .Q(line_26), .clk(memoryupdater_15_hupdate));  // open: en, clr
  Register #(.width(32)) register_34 (.D(register_24_q), .Q(line_30), .clk(memoryupdater_16_hupdate));  // open: en, clr
  not not_1 (not_1_out, and_3_out);
  not not_2 (not_2_out, not_1_out);
  not not_3 (not_3_out, not_2_out);
  not not_4 (not_4_out, not_3_out);
  Register #(.width(32)) register_35 (
    .D({register_25_q, register_26_q}), .Q(register_35_q), .clk(HSEL_3));  // open: en, clr
  MemoryUpdater memoryupdater_17 (.HSEL(HSEL_3), .HUPT(HUPT), .HUPDATE(memoryupdater_17_hupdate));
  Register #(.width(32)) register_36 (
    .D({register_25_q, register_26_q}), .Q(register_36_q), .clk(HSEL_7));  // open: en, clr
  MemoryUpdater memoryupdater_18 (.HSEL(HSEL_7), .HUPT(HUPT), .HUPDATE(memoryupdater_18_hupdate));
  Register #(.width(32)) register_37 (
    .D({register_25_q, register_26_q}), .Q(register_37_q), .clk(HSEL_11));  // open: en, clr
  MemoryUpdater memoryupdater_19 (.HSEL(HSEL_11), .HUPT(HUPT), .HUPDATE(memoryupdater_19_hupdate));
  Register #(.width(32)) register_38 (
    .D({register_25_q, register_26_q}), .Q(register_38_q), .clk(HSEL_15));  // open: en, clr
  MemoryUpdater memoryupdater_20 (.HSEL(HSEL_15), .HUPT(HUPT), .HUPDATE(memoryupdater_20_hupdate));
  Register #(.width(32)) register_39 (
    .D({register_25_q, register_26_q}), .Q(register_39_q), .clk(HSEL_19));  // open: en, clr
  MemoryUpdater memoryupdater_21 (.HSEL(HSEL_19), .HUPT(HUPT), .HUPDATE(memoryupdater_21_hupdate));
  Register #(.width(32)) register_40 (
    .D({register_25_q, register_26_q}), .Q(register_40_q), .clk(HSEL_23));  // open: en, clr
  MemoryUpdater memoryupdater_22 (.HSEL(HSEL_23), .HUPT(HUPT), .HUPDATE(memoryupdater_22_hupdate));
  Register #(.width(32)) register_41 (
    .D({register_25_q, register_26_q}), .Q(register_41_q), .clk(HSEL_27));  // open: en, clr
  MemoryUpdater memoryupdater_23 (.HSEL(HSEL_27), .HUPT(HUPT), .HUPDATE(memoryupdater_23_hupdate));
  Register #(.width(32)) register_42 (
    .D({register_25_q, register_26_q}), .Q(register_42_q), .clk(HSEL_31));  // open: en, clr
  MemoryUpdater memoryupdater_24 (.HSEL(HSEL_31), .HUPT(HUPT), .HUPDATE(memoryupdater_24_hupdate));
  Register #(.width(32)) register_43 (.D(register_35_q), .Q(line_3), .clk(memoryupdater_17_hupdate));  // open: en, clr
  Register #(.width(32)) register_44 (.D(register_36_q), .Q(line_7), .clk(memoryupdater_18_hupdate));  // open: en, clr
  Register #(.width(32)) register_45 (.D(register_37_q), .Q(line_11), .clk(memoryupdater_19_hupdate));  // open: en, clr
  Register #(.width(32)) register_46 (.D(register_38_q), .Q(line_15), .clk(memoryupdater_20_hupdate));  // open: en, clr
  Register #(.width(32)) register_47 (.D(register_39_q), .Q(line_19), .clk(memoryupdater_21_hupdate));  // open: en, clr
  Register #(.width(32)) register_48 (.D(register_40_q), .Q(line_23), .clk(memoryupdater_22_hupdate));  // open: en, clr
  Register #(.width(32)) register_49 (.D(register_41_q), .Q(line_27), .clk(memoryupdater_23_hupdate));  // open: en, clr
  Register #(.width(32)) register_50 (.D(register_42_q), .Q(line_31), .clk(memoryupdater_24_hupdate));  // open: en, clr
  Demultiplexer #(.select(5)) demultiplexer_2 (
    .out0(HSEL_1), .out1(HSEL_2), .out2(HSEL_3), .out3(HSEL_4), .out4(HSEL_5), .out5(HSEL_6), .out6(HSEL_7),
    .out7(HSEL_8), .out8(HSEL_9), .out9(HSEL_10), .out10(HSEL_11), .out11(HSEL_12), .out12(HSEL_13),
    .out13(HSEL_14), .out14(HSEL_15), .out15(HSEL_16), .out16(HSEL_17), .out17(HSEL_18), .out18(HSEL_19),
    .out19(HSEL_20), .out20(HSEL_21), .out21(HSEL_22), .out22(HSEL_23), .out23(HSEL_24), .out24(HSEL_25),
    .out25(HSEL_26), .out26(HSEL_27), .out27(HSEL_28), .out28(HSEL_29), .out29(HSEL_30), .out30(HSEL_31),
    .out31(HSEL_32), .in(not_4_out), .sel(HADDR_7_0[6:2]));  // open: en
  Register #(.width(32)) register_51 (
    .D({register_25_q, register_26_q}), .Q(register_51_q), .clk(HSEL_4));  // open: en, clr
  MemoryUpdater memoryupdater_25 (.HSEL(HSEL_4), .HUPT(HUPT), .HUPDATE(memoryupdater_25_hupdate));
  Register #(.width(32)) register_52 (
    .D({register_25_q, register_26_q}), .Q(register_52_q), .clk(HSEL_8));  // open: en, clr
  MemoryUpdater memoryupdater_26 (.HSEL(HSEL_8), .HUPT(HUPT), .HUPDATE(memoryupdater_26_hupdate));
  Register #(.width(32)) register_53 (
    .D({register_25_q, register_26_q}), .Q(register_53_q), .clk(HSEL_12));  // open: en, clr
  MemoryUpdater memoryupdater_27 (.HSEL(HSEL_12), .HUPT(HUPT), .HUPDATE(memoryupdater_27_hupdate));
  Register #(.width(32)) register_54 (
    .D({register_25_q, register_26_q}), .Q(register_54_q), .clk(HSEL_16));  // open: en, clr
  MemoryUpdater memoryupdater_28 (.HSEL(HSEL_16), .HUPT(HUPT), .HUPDATE(memoryupdater_28_hupdate));
  Register #(.width(32)) register_55 (
    .D({register_25_q, register_26_q}), .Q(register_55_q), .clk(HSEL_20));  // open: en, clr
  MemoryUpdater memoryupdater_29 (.HSEL(HSEL_20), .HUPT(HUPT), .HUPDATE(memoryupdater_29_hupdate));
  Register #(.width(32)) register_56 (
    .D({register_25_q, register_26_q}), .Q(register_56_q), .clk(HSEL_24));  // open: en, clr
  MemoryUpdater memoryupdater_30 (.HSEL(HSEL_24), .HUPT(HUPT), .HUPDATE(memoryupdater_30_hupdate));
  Register #(.width(32)) register_57 (
    .D({register_25_q, register_26_q}), .Q(register_57_q), .clk(HSEL_28));  // open: en, clr
  MemoryUpdater memoryupdater_31 (.HSEL(HSEL_28), .HUPT(HUPT), .HUPDATE(memoryupdater_31_hupdate));
  Register #(.width(32)) register_58 (
    .D({register_25_q, register_26_q}), .Q(register_58_q), .clk(HSEL_32));  // open: en, clr
  MemoryUpdater memoryupdater_32 (.HSEL(HSEL_32), .HUPT(HUPT), .HUPDATE(memoryupdater_32_hupdate));
  Register #(.width(32)) register_59 (.D(register_51_q), .Q(line_4), .clk(memoryupdater_25_hupdate));  // open: en, clr
  Register #(.width(32)) register_60 (.D(register_52_q), .Q(line_8), .clk(memoryupdater_26_hupdate));  // open: en, clr
  Register #(.width(32)) register_61 (.D(register_53_q), .Q(line_12), .clk(memoryupdater_27_hupdate));  // open: en, clr
  Register #(.width(32)) register_62 (.D(register_54_q), .Q(line_16), .clk(memoryupdater_28_hupdate));  // open: en, clr
  Register #(.width(32)) register_63 (.D(register_55_q), .Q(line_20), .clk(memoryupdater_29_hupdate));  // open: en, clr
  Register #(.width(32)) register_64 (.D(register_56_q), .Q(line_24), .clk(memoryupdater_30_hupdate));  // open: en, clr
  Register #(.width(32)) register_65 (.D(register_57_q), .Q(line_28), .clk(memoryupdater_31_hupdate));  // open: en, clr
  Register #(.width(32)) register_66 (.D(register_58_q), .Q(line_32), .clk(memoryupdater_32_hupdate));  // open: en, clr

  // Notes on the sheet:
  //   Merging two 16-bit string transactions into a 32-bit string
  //   Distribution of 32-bit string into blocks
  //   Slave main display showing gallows pictures
endmodule

module MemoryUpdater (
  input  HSEL,
  input  HUPT,
  output HUPDATE
);

  wire and_1_out, and_2_out, d_ff_1_q, not_1_out, not_2_out, not_3_out, not_4_out, not_6_out, or_1_out;

  and and_1 (and_1_out, HSEL, HUPT);
  D_Flip_Flop d_ff_1 (.clk(HUPT), .D(HUPT), .Q(d_ff_1_q), .reset(and_2_out));  // open: Qn, preset, en
  or or_1 (or_1_out, and_1_out, and_2_out);
  and and_2 (and_2_out, HUPT, d_ff_1_q);
  not not_1 (not_1_out, or_1_out);
  not not_2 (not_2_out, not_1_out);
  not not_3 (not_3_out, not_2_out);
  not not_4 (not_4_out, not_3_out);
  not not_5 (HUPDATE, not_6_out);
  not not_6 (not_6_out, not_4_out);

  // Notes on the sheet:
  //   Block of instant signal for updating displays
endmodule
